// Logisim project ALU.circ as structural Verilog: 8 circuits, main circuit ALU
module ALU (
  input  [31:0] X,
  input  [31:0] Y,
  input  [3:0] AluOP,
  output Signed_Overflow,
  output UnSigned_Overflow,
  output Equal,
  output [31:0] Result,
  output [31:0] Result_2
);

  wire adder_1_cout, adder_2_out, and_1_out, comparator_1_lt, comparator_2_lt, not_1_out, not_2_out,
       xor_1_out, xor_4_out, xor_5_out;
  wire [2:0] and_3_out, bit_extender_2_out;
  wire [31:0] adder_1_out, and_2_out, bit_extender_1_out, bit_extender_3_out, bit_extender_4_out,
       divider_1_out, divider_1_rem, multiplier_1_cout, multiplier_1_out, not_3_out, or_1_out, shifter_1_out,
       shifter_2_out, shifter_3_out, xor_2_out, xor_3_out;

  // Probe on X
  // Probe on X
  xor xor_1 (xor_1_out, AluOP[0], AluOP[1]);
  not not_1 (not_1_out, AluOP[3]);
  assign bit_extender_1_out = {{31{AluOP[1]}}, AluOP[1]};  // Bit_Extender bit_extender_1
  // Probe on Y
  // Probe on Y
  not not_2 (not_2_out, AluOP[3]);
  Shifter #(.width(32)) shifter_1 (.in(X), .\dist (Y[4:0]), .out(shifter_1_out));
  Shifter #(.width(32), .shift("ar")) shifter_2 (.in(X), .\dist (Y[4:0]), .out(shifter_2_out));
  Shifter #(.width(32), .shift("lr")) shifter_3 (.in(X), .\dist (Y[4:0]), .out(shifter_3_out));
  Multiplier #(.width(32)) multiplier_1 (.a(X), .b(Y), .out(multiplier_1_out), .cout(multiplier_1_cout));  // open: cin
  Divider #(.width(32)) divider_1 (.a(X), .b(Y), .out(divider_1_out), .rem(divider_1_rem));  // open: upper
  and and_1 (and_1_out, xor_1_out, AluOP[2], not_1_out);
  assign xor_2_out = bit_extender_1_out ^ Y;  // XOR_Gate xor_2, 32 bits wide
  assign and_2_out = X & Y;  // AND_Gate and_2, 32 bits wide
  assign or_1_out = X | Y;  // OR_Gate or_1, 32 bits wide
  assign xor_3_out = X ^ Y;  // XOR_Gate xor_3, 32 bits wide
  Comparator #(.width(32)) comparator_1 (.a(X), .b(Y), .lt(comparator_1_lt));  // open: gt, eq
  Comparator #(.width(32), .mode("unsigned")) comparator_2 (
    .a(X), .b(Y), .eq(Equal), .lt(comparator_2_lt));  // open: gt
  // Probe on AluOP
  assign bit_extender_2_out = {{2{not_2_out}}, not_2_out};  // Bit_Extender bit_extender_2
  // Probe on Result
  // Probe on Result
  assign and_3_out = bit_extender_2_out & AluOP[2:0];  // AND_Gate and_3, 3 bits wide
  Adder #(.width(32)) adder_1 (.a(xor_2_out), .b(X), .out(adder_1_out), .cin(AluOP[1]), .cout(adder_1_cout));
  Adder #(.width(1)) adder_2 (.a(xor_2_out[31]), .b(X[31]), .out(adder_2_out), .cin(adder_1_cout));  // open: cout
  assign not_3_out = ~or_1_out;  // NOT_Gate not_3, 32 bits wide
  assign bit_extender_3_out = {{31{1'b0}}, comparator_1_lt};  // Bit_Extender bit_extender_3
  assign bit_extender_4_out = {{31{1'b0}}, comparator_2_lt};  // Bit_Extender bit_extender_4
  // Probe on Result_2
  Multiplexer #(.select(3), .width(32), .enable("false")) multiplexer_1 (
    .in0({32{1'b0}}), .in1({32{1'b0}}), .in2({32{1'b0}}), .in3(multiplier_1_cout), .in4(divider_1_rem),
    .in5({32{1'b0}}), .in6({32{1'b0}}), .in7({32{1'b0}}), .out(Result_2), .sel(and_3_out));
  xor xor_4 (xor_4_out, adder_1_out[31], adder_2_out);
  xor xor_5 (xor_5_out, adder_1_cout, AluOP[1]);
  and and_4 (Signed_Overflow, and_1_out, xor_4_out);
  and and_5 (UnSigned_Overflow, and_1_out, xor_5_out);
  Multiplexer #(.select(4), .width(32), .enable("false")) multiplexer_2 (
    .in0(shifter_1_out), .in1(shifter_2_out), .in2(shifter_3_out), .in3(multiplier_1_out),
    .in4(divider_1_out), .in5(adder_1_out), .in6(adder_1_out), .in7(and_2_out), .in8(or_1_out),
    .in9(xor_3_out), .in10(not_3_out), .in11(bit_extender_3_out), .in12(bit_extender_4_out),
    .in13({32{1'b0}}), .in14({32{1'b0}}), .in15({32{1'b0}}), .out(Result), .sel(AluOP));

  // Other names for the same wires on the sheet: CF = UnSigned_Overflow; OF = Signed_Overflow;
  //   Result2[31:0] = Result_2; S[3:0] = AluOP

  // Notes on the sheet:
  //   不要改变此引脚区域内容，也不要改变ALU封装形式
  //   输入引脚
  //   请在下方利用上方输入输出引脚的隧道信号构建ALU电路，ctrl+d复制选择部件
  //   输出引脚
  //   探测区域
endmodule

module \演示电路  (
  input  [31:0] X,
  input  [31:0] Y,
  input  [3:0] ALUOP,
  output Signed_Overflow,
  output Unsigned_overflow,
  output [31:0] Result,
  output [31:0] Result_2,
  output Equal
);

  // Probe on X
  // Probe on X
  ALU alu_1 (
    .AluOP(ALUOP), .X(X), .Equal(Equal), .Result(Result), .Signed_Overflow(Signed_Overflow), .Y(Y),
    .Result_2(Result_2), .UnSigned_Overflow(Unsigned_overflow));
  // Probe on ALUOP
  // Probe on Y
  // Probe on Y
  // Probe on Result
  // Probe on Result
  // Probe on Result_2
endmodule

module \毛刺现象  (
  input  in_1
);

  wire and_1_out, not_1_out;

  not not_1 (not_1_out, in_1);
  and and_1 (and_1_out, in_1, not_1_out);
  Counter counter_1 (.clk(and_1_out));  // open: load, D, count, Q, carry, clr

  // Notes on the sheet:
  //   尝试反复点击输入引脚改变值，观察计算器的变化
  //   逻辑上应该为零，但计数器观察到了跳变
endmodule

module \震荡电路  (
  input  in_1,
  output out_2
);

  nand nand_1 (out_2, in_1, out_2);

  // Notes on the sheet:
  //   尝试修改输入引脚的电平,输入输出存在反馈，导致电路状态不稳定
  //   如出现类似情况，尝试去掉部分回路连接直至故障消除
  //   华中科技大学计算机学院 计算机组成原理
endmodule

module \信号冲突  (
  input  in_1,
  input  in_2,
  output out_3
);


  assign in_2 = in_1;
  assign out_3 = in_1;

  // Notes on the sheet:
  //   输入相同时无问题，不同时出错，红色显示
  //   华中科技大学计算机学院 计算机组成原理
endmodule

module \等差数列求和  (
  input  in_1,
  input  [31:0] \等差值 ,
  input  [31:0] \初始值 
);

  wire clock, not_1_out, register_1_q;
  wire [3:0] alu_2_result_2, alu_2_result_3;
  wire [23:0] alu_2_result;
  wire [31:0] alu_1_result, and_1_out, bit_extender_1_out, or_1_out, or_2_out, register_2_q, register_3_q;

  Clock clock_1 (.out(clock));
  Register #(.width(1)) register_1 (.D(1'b1), .Q(register_1_q), .clk(clock), .clr(in_1));  // open: en
  not not_1 (not_1_out, register_1_q);
  assign bit_extender_1_out = {{31{not_1_out}}, not_1_out};  // Bit_Extender bit_extender_1
  assign and_1_out = \初始值  & bit_extender_1_out;  // AND_Gate and_1, 32 bits wide
  assign or_1_out = and_1_out | register_2_q;  // OR_Gate or_1, 32 bits wide
  assign or_2_out = and_1_out | register_3_q;  // OR_Gate or_2, 32 bits wide
  ALU alu_1 (
    .AluOP(4'b0101), .X(\等差值 ), .Result(alu_1_result), .Y(or_1_out));  // open: Equal, Signed_Overflow, Result_2, UnSigned_Overflow
  Register #(.width(32)) register_2 (.D(alu_1_result), .Q(register_2_q), .clk(clock), .clr(in_1));  // open: en
  Hex_Digit_Display hex_digit_display_1 (.value(alu_2_result_3));  // open: dp
  Hex_Digit_Display hex_digit_display_2 (.value(alu_2_result_2));  // open: dp
  ALU alu_2 (
    .AluOP(4'b0101), .X(register_2_q), .Result({alu_2_result_3, alu_2_result_2, alu_2_result}), .Y(or_2_out));  // open: Equal, Signed_Overflow, Result_2, UnSigned_Overflow
  Hex_Digit_Display hex_digit_display_3 (.value(alu_2_result[23:20]));  // open: dp
  Hex_Digit_Display hex_digit_display_4 (.value(alu_2_result[19:16]));  // open: dp
  Register #(.width(32)) register_3 (
    .D({alu_2_result_3, alu_2_result_2, alu_2_result}), .Q(register_3_q), .clk(clock), .clr(in_1));  // open: en
  Hex_Digit_Display hex_digit_display_5 (.value(alu_2_result[11:8]));  // open: dp
  Hex_Digit_Display hex_digit_display_6 (.value(alu_2_result[15:12]));  // open: dp
  Hex_Digit_Display hex_digit_display_7 (.value(alu_2_result[7:4]));  // open: dp
  Hex_Digit_Display hex_digit_display_8 (.value(alu_2_result[3:0]));  // open: dp
  // Probe on {alu_2_result_3, alu_2_result_2, alu_2_result}

  // Other names for the same wires on the sheet: reset = in_1
endmodule

module \不同颜色信号线  (
  input  \引脚类型不对 ,
  input  [1:0] in_2,
  input  in_3
);

  wire undriven;
  wire [1:0] nand_2_out, undriven_3;
  wire [1:1] undriven_2;

  nand nand_1 (\引脚类型不对 , 1'b1, 1'b0, undriven, 1'b0);
  assign nand_2_out = ~(in_2 & undriven_3 & {undriven_2[1], in_3});  // NAND_Gate nand_2, 2 bits wide
  // Pins of 1 and 2 bits meet at {undriven_2[1], in_3}

  // Notes on the sheet:
  //   深绿色表示高电平
  //   蓝色表示未知状态
  //   灰色表示飞线
  //   亮绿色表示高电平
  //   红色表示信号冲突
  //   黑色表示多位总线
  //   橙色表示位宽不匹配
  //   华中科技大学计算机学院 计算机组成原理
endmodule

module \分线器使用  (
  input  [7:0] in_1
);


  // Notes on the sheet:
  //   分线器使用方法
  //   8分3，两个3位，一个2位
  //   分线器不分输入输出，可反向使用进行线缆汇总
  //   华中科技大学计算机学院 计算机组成原理
  //   8分二，高位在下
  //   8分二，高位在上
  //   只分部分位，位宽不对称
  //   只分1位，如取符号位
  //   8分8
endmodule
