// Logisim project RedirectionPipelineCPU.circ as structural Verilog: 12 circuits, main circuit main
module main (
);

  wire _1_out, alu_2_p4, branch, clear, clock, clock_1_out, comparator_1_eq, control_1_aluscra,
       control_1_eret, control_1_memwrite, control_1_regwrite, control_1_rs, control_1_rt, control_1_syscall,
       ERET, ex_mem_1_eret_2, ex_mem_1_memwrite_2, ex_mem_1_syscall_2, exe, Halt, id_ex_1_aluscra_2,
       id_ex_1_eret_2, id_ex_1_memwrite_2, id_ex_1_regwrite_2, IE, intr, JAL, LockB, LockD, mem_wb_1_p7,
       mem_wb_1_p15, MToRE, nand_1_out, not_1_out, npc_1_success, or_1_out, or_2_out, or_3_out, or_4_out,
       or_5_out, or_6_out, register_3_q, RS, RT, RW, RWM, Singed, syscall, syscallE;
  wire [1:0] control_1_alusrcb, control_1_dinop, control_1_pcop, control_1_w_op, ex_mem_1_dinop_2,
       hazard_1_forwardae, hazard_1_forwardbe, id_ex_1_aluscrb_2, id_ex_1_pcop_2, id_ex_1_w_op_2,
       mem_wb_1_p18, W_op, W_opM;
  wire [3:0] Aluop, control_1_aluop, register_1_q_2;
  wire [4:0] ex_mem_1_rd_2, ex_mem_1_rs_2, ex_mem_1_rt_2, id_ex_1_rd_2, id_ex_1_rs_4, id_ex_1_rt_4, rd, rt_t,
       translator_1_r1_num, translator_1_r2_num, translator_1_w_num;
  wire [15:0] counter_1_bub, counter_1_per, instructions_1_all, instructions_1_i_type, instructions_1_j_type,
       instructions_1_r_type;
  wire [27:0] register_1_q;
  wire [31:0] a0, ALU, alu_2_p5, bit_extender_1_out, bit_extender_2_out, bit_extender_3_out, Din, EPC_q,
       ex_mem_1_d2_2, ex_mem_1_ir_2, ex_mem_1_pcout, id_ex_1_d1out, id_ex_1_d2out, id_ex_1_ir10_6_2,
       id_ex_1_ir15_0_2, id_ex_1_ir_2, id_ex_1_pcout, if_id_1_irout, if_id_1_pcout, main_1_p9, main_1_p10,
       MEM, mem_wb_1_p14, mem_wb_1_p21, multiplexer_1_out, multiplexer_2_out, multiplexer_3_out,
       multiplexer_4_out, multiplexer_5_out, multiplexer_6_out, multiplexer_7_out, NPC, PC, PC_4, ram_1_data,
       rom_1_data, v0;
  wire [31:26] IR;

  or or_1 (or_1_out, ~LockD, LockB);  // OR_Gate
  Hex_Digit_Display hex_digit_display_1 (.value(register_1_q_2));  // open: dp
  Register #(.width(32)) register_1 (
    .D(a0), .en(syscall), .Q({register_1_q_2, register_1_q}), .clk(clock));  // open: clr
  Register #(.width(32)) u_PC (.D(NPC), .en(or_1_out), .Q(PC), .clk(clock));  // open: clr
  Hex_Digit_Display hex_digit_display_2 (.value(register_1_q[23:20]));  // open: dp
  Hex_Digit_Display hex_digit_display_3 (.value(register_1_q[27:24]));  // open: dp
  // ALU alu_1: pin names not known; wires that end beside it: 32'h4, PC, 4'b0101, PC_4
  Hex_Digit_Display hex_digit_display_4 (.value(register_1_q[15:12]));  // open: dp
  Hex_Digit_Display hex_digit_display_5 (.value(register_1_q[19:16]));  // open: dp
  IF_ID if_id_1 (
    .PCin(PC_4), .IRin(rom_1_data), .PCout(if_id_1_pcout), .IRout(if_id_1_irout), .Clock(clock),
    .EN(or_1_out), .branch(branch));
  ROM #(.addrWidth(10), .dataWidth(32)) rom_1 (.addr(PC[11:2]), .data(rom_1_data));  // open: sel
  Hex_Digit_Display hex_digit_display_6 (.value(register_1_q[7:4]));  // open: dp
  Hex_Digit_Display hex_digit_display_7 (.value(register_1_q[11:8]));  // open: dp
  Hex_Digit_Display hex_digit_display_8 (.value(register_1_q[3:0]));  // open: dp
  Control control_1 (
    .op(if_id_1_irout[31:26]), .PCop(control_1_pcop), .SingnedIMM(Singed), .ALUop(control_1_aluop),
    .AluScrA(control_1_aluscra), .MemWrite(control_1_memwrite), .RegWrite(control_1_regwrite),
    .ERET(control_1_eret), .fun(if_id_1_irout[5:0]), .M(if_id_1_irout[25:21]), .W_op(control_1_w_op),
    .Syscall(control_1_syscall), .Dinop(control_1_dinop), .AluSrcB(control_1_alusrcb), .RS(control_1_rs),
    .RT(control_1_rt));
  Translator translator_1 (
    .IR(if_id_1_irout), .ERET(control_1_eret), .exe(exe), .rd(rd), .rt(rt_t), .R1_num(translator_1_r1_num),
    .R2_num(translator_1_r2_num), .W_num(translator_1_w_num), .W_op(W_op));
  Counter counter_1 (.BUb(counter_1_bub), .Per(counter_1_per), .syscall(Halt), .clock(clock), .LOCK(LockD));
  Button _1 (.out(_1_out));
  assign bit_extender_1_out = {{16{1'b0}}, if_id_1_irout[15:0]};  // Bit_Extender bit_extender_1
  assign bit_extender_2_out = {{16{if_id_1_irout[15]}}, if_id_1_irout[15:0]};  // Bit_Extender bit_extender_2
  assign bit_extender_3_out = {{27{1'b0}}, if_id_1_irout[10:6]};  // Bit_Extender bit_extender_3
  // Probe on counter_1_bub
  // Probe on counter_1_per
  Register #(.width(1)) register_2 (.D(_1_out), .Q(exe), .clk(clock));  // open: en, clr
  not not_1 (not_1_out, clock);
  Multiplexer #(.width(32), .enable("false")) multiplexer_1 (
    .in0(bit_extender_1_out), .in1(bit_extender_2_out), .out(multiplexer_1_out), .sel(Singed));
  Register #(.width(1)) register_3 (.D(1'b1), .Q(register_3_q), .clk(exe), .clr(ERET));  // open: en
  Register #(.width(1)) u_IE (.D(1'b1), .en(or_2_out), .Q(IE), .clk(clock), .clr(intr));
  or or_2 (or_2_out, ~intr, ERET);  // OR_Gate
  // Probe on rom_1_data
  ID_EX id_ex_1 (
    .PCin(if_id_1_pcout), .D1(main_1_p9), .D2(main_1_p10), .IR15_0(multiplexer_1_out),
    .IR10_6(bit_extender_3_out), .PCout(id_ex_1_pcout), .D1out(id_ex_1_d1out), .D2out(id_ex_1_d2out),
    .IR15_0_2(id_ex_1_ir15_0_2), .IR10_6_2(id_ex_1_ir10_6_2), .Clock(clock), .IR(if_id_1_irout),
    .IR_2(id_ex_1_ir_2), .rt_2(if_id_1_irout[20:16]), .rt_4(id_ex_1_rt_4), .rd(if_id_1_irout[15:11]),
    .rd_2(id_ex_1_rd_2), .syscall(control_1_syscall), .syscall_2(syscallE), .ERET(control_1_eret),
    .ERET_2(id_ex_1_eret_2), .RegWrite(control_1_regwrite), .RegWrite_2(id_ex_1_regwrite_2),
    .W_op(control_1_w_op), .W_op_2(id_ex_1_w_op_2), .Dinop(control_1_dinop), .Dinop_2({MToRE, JAL}),
    .MemWrite(control_1_memwrite), .MemWrite_2(id_ex_1_memwrite_2), .PCop(control_1_pcop),
    .PCop_2(id_ex_1_pcop_2), .ALUop(control_1_aluop), .ALUop_2(Aluop), .AluScrB(control_1_alusrcb),
    .AluScrB_2(id_ex_1_aluscrb_2), .AluScrA(control_1_aluscra), .AluScrA_2(id_ex_1_aluscra_2),
    .rs_2(if_id_1_irout[25:21]), .rs_4(id_ex_1_rs_4), .RT(control_1_rt), .RT_3(RT), .RS(control_1_rs),
    .RS_3(RS), .hazard(clear), .branch(branch));
  // 韩云_CS1307_U201314999_Regfile_main main_1: pin names not known; wires that end beside it: translator_1_r1_num, translator_1_r2_num, translator_1_w_num, Din, RW, v0, not_1_out, a0, main_1_p9, main_1_p10, branch
  Hazard hazard_1 (
    .rtM(ex_mem_1_rt_2), .rdM(ex_mem_1_rd_2), .W_opM(W_opM), .RegWriteM(RWM), .RS(RS), .RT(RT),
    .rsE(id_ex_1_rs_4), .rtE(id_ex_1_rt_4), .RegWriteW(RW), .rdW(rd), .rtW(rt_t), .W_opW(W_op),
    .ForwardAE(hazard_1_forwardae), .ForwardBE(hazard_1_forwardbe), .FlushE(LockD), .MemToRegE(MToRE),
    .rsD(if_id_1_irout[25:21]), .rtD(if_id_1_irout[20:16]), .BranchHazard(LockB), .PCop(id_ex_1_pcop_2),
    .success(npc_1_success));
  Register #(.width(1)) register_4 (.D(register_3_q), .Q(intr), .clk(clock));  // open: en, clr
  // Probe on if_id_1_irout
  // Probe on id_ex_1_ir_2
  NPC npc_1 (
    .PC_4(PC_4), .PC(id_ex_1_pcout), .IMM16(id_ex_1_ir15_0_2), .IR(id_ex_1_ir_2), .Equal(alu_2_p4),
    .D1(id_ex_1_d1out), .NPC(NPC), .PCop(id_ex_1_pcop_2), .ERET(id_ex_1_eret_2), .exe(exe), .MEM(MEM),
    .success(npc_1_success));
  // Probe on ex_mem_1_ir_2
  Multiplexer #(.select(2), .width(32), .enable("false")) multiplexer_2 (
    .in0(id_ex_1_d2out), .in1(Din), .in2(ALU), .in3(ALU), .out(multiplexer_2_out), .sel(hazard_1_forwardbe));
  Instructions instructions_1 (
    .op(IR), .clock(clock), .in_3(Halt), .R_type(instructions_1_r_type), .I_type(instructions_1_i_type),
    .J_type(instructions_1_j_type), .ALL(instructions_1_all));
  // Probe on mem_wb_1_p15
  Multiplexer #(.select(2), .width(32), .enable("false")) multiplexer_3 (
    .in0(id_ex_1_d1out), .in1(Din), .in2(ALU), .in3(ALU), .out(multiplexer_3_out), .sel(hazard_1_forwardae));
  Multiplexer #(.select(2), .width(32), .enable("false")) multiplexer_4 (
    .in0(id_ex_1_ir15_0_2), .in1(id_ex_1_ir10_6_2), .in2(multiplexer_2_out), .in3(32'ha),
    .out(multiplexer_4_out), .sel(id_ex_1_aluscrb_2));
  // Probe on instructions_1_r_type
  // Probe on instructions_1_i_type
  // Probe on instructions_1_j_type
  // Probe on instructions_1_all
  or or_3 (or_3_out, id_ex_1_aluscra_2, or_4_out);
  or or_4 (or_4_out, id_ex_1_eret_2, exe);
  Multiplexer #(.width(32), .enable("false")) multiplexer_5 (
    .in0(multiplexer_4_out), .in1({32{1'b0}}), .out(multiplexer_5_out), .sel(or_4_out));
  Register #(.width(1)) register_5 (.D(LockD), .Q(clear), .clk(clock), .clr(clear));  // open: en
  Multiplexer #(.width(32), .enable("false")) multiplexer_6 (
    .in0(multiplexer_3_out), .in1(multiplexer_2_out), .out(multiplexer_6_out), .sel(or_3_out));
  EX_MEM ex_mem_1 (
    .PCin(id_ex_1_pcout), .IR(id_ex_1_ir_2), .ALU(alu_2_p5), .D2(multiplexer_2_out), .PCout(ex_mem_1_pcout),
    .IR_2(ex_mem_1_ir_2), .ALU_2(ALU), .D2_2(ex_mem_1_d2_2), .Clock(clock), .rt(id_ex_1_rt_4),
    .rt_2(ex_mem_1_rt_2), .rd(id_ex_1_rd_2), .rd_2(ex_mem_1_rd_2), .RegWrite(id_ex_1_regwrite_2),
    .RegWrite_2(RWM), .MemWrite(id_ex_1_memwrite_2), .MemWrite_2(ex_mem_1_memwrite_2), .syscall(syscallE),
    .syscall_2(ex_mem_1_syscall_2), .Dinop({MToRE, JAL}), .Dinop_2(ex_mem_1_dinop_2), .ERET(id_ex_1_eret_2),
    .ERET_2(ex_mem_1_eret_2), .W_op(id_ex_1_w_op_2), .W_op_2(W_opM), .rs(id_ex_1_rs_4), .rs_2(ex_mem_1_rs_2));
  // ALU alu_2: pin names not known; wires that end beside it: multiplexer_6_out, multiplexer_5_out, Aluop, alu_2_p4, alu_2_p5
  Register #(.width(1)) register_6 (.D(LockB), .Q(branch), .clk(clock), .clr(branch));  // open: en
  Multiplexer #(.width(32), .enable("false")) multiplexer_7 (
    .in0(ex_mem_1_d2_2), .in1(EPC_q), .out(multiplexer_7_out), .sel(exe));
  Register #(.width(32)) EPC (.D(PC), .Q(EPC_q), .clk(exe));  // open: en, clr
  or or_5 (or_5_out, ex_mem_1_memwrite_2, exe);
  RAM #(.addrWidth(10), .dataWidth(32), .bus("separate")) ram_1 (
    .addr(ALU[11:2]), .din(multiplexer_7_out), .data(ram_1_data), .str(or_5_out), .clk(clock), .ld(or_6_out));  // open: sel, clr
  or or_6 (or_6_out, ex_mem_1_dinop_2[1], ex_mem_1_eret_2);
  // MEM_WB mem_wb_1: pin names not known; wires that end beside it: ex_mem_1_pcout, ex_mem_1_ir_2, RWM, W_opM, ex_mem_1_dinop_2, ex_mem_1_syscall_2, mem_wb_1_p7, ALU, ram_1_data, ex_mem_1_rs_2, ex_mem_1_rt_2, ex_mem_1_rd_2, clock, mem_wb_1_p14, mem_wb_1_p15, RW, W_op, mem_wb_1_p18, syscall, mem_wb_1_p7, mem_wb_1_p21, MEM, rt_t, rd
  Multiplexer #(.select(2), .width(32), .enable("false")) multiplexer_8 (
    .in0(mem_wb_1_p21), .in1(mem_wb_1_p14), .in2(MEM), .in3(MEM), .out(Din), .sel(mem_wb_1_p18));
  Comparator #(.width(32)) comparator_1 (.a(v0), .b(32'ha), .eq(comparator_1_eq));  // open: gt, lt
  nand nand_1 (nand_1_out, syscall, comparator_1_eq);
  Clock clock_1 (.out(clock_1_out));
  not not_2 (Halt, nand_1_out);
  Counter_part #(.width(1), .max('h1)) counter_2 (
    .count(nand_1_out), .Q(clock), .clk(clock_1_out));  // open: load, D, carry, clr

  // Notes on the sheet:
  //   contents of rom_1 (hex, n*v repeats v):
  //   20110001 8000c05 20110001 20120002 20130003 8000c09 20110001 20120002 20130003 8000c0d 20110001
  //   20120002 20130003 8000c11 20110001 20120002 20130003 c000cb8 20100001 20110001 118fc0 112020
  //   20020022 c 118882 12200001 8000c15 112020 20020022 c 20110001 118880 112020 20020022 c 12200001
  //   8000c1f 20110001 118fc0 112020 20020022 c 1188c3 112020 20020022 c 118903 112020 20020022 c 118903
  //   112020 20020022 c 118903 112020 20020022 c 118903 112020 20020022 c 118903 112020 20020022 c 118903
  //   112020 20020022 c 118903 112020 20020022 c 20100001 109fc0 139fc3 8021 2012000c 24160003 26100001
  //   3210000f 20080008 20090001 139900 2709825 132020 20020022 c 1094022 1500fff9 22100001 2018000f
  //   2188024 108700 20080008 20090001 139902 2709825 132021 20020022 c 1094022 1500fff9 108702 2c9b022
  //   12c00001 8000c50 4020 1084027 84400 3508ffff 82021 20020022 c 2010ffff 20110000 ae300000 22100001
  //   22310004 ae300000 22100001 22310004 ae300000 22100001 22310004 ae300000 22100001 22310004 ae300000
  //   22100001 22310004 ae300000 22100001 22310004 ae300000 22100001 22310004 ae300000 22100001 22310004
  //   ae300000 22100001 22310004 ae300000 22100001 22310004 ae300000 22100001 22310004 ae300000 22100001
  //   22310004 ae300000 22100001 22310004 ae300000 22100001 22310004 ae300000 22100001 22310004 ae300000
  //   22100001 22310004 22100001 8020 2011003c 8e130000 8e340000 274402a 11000002 ae330000 ae140000
  //   2231fffc 1611fff8 102020 20020022 c 22100004 2011003c 1611fff2 2002000a c 20100000 22100001 102020
  //   20020022 c 22100002 102020 20020022 c 22100003 102020 20020022 c 22100004 102020 20020022 c 22100005
  //   102020 20020022 c 22100006 102020 20020022 c 22100007 102020 20020022 c 22100008 102020 20020022
  //   20020022 c 3e00008
  //   Display
endmodule

module Control (
  input  [5:0] op,
  input  [5:0] fun,
  input  [4:0] M,
  output RegWrite,
  output [1:0] PCop,
  output SingnedIMM,
  output Syscall,
  output AluScrA,
  output [3:0] ALUop,
  output [1:0] AluSrcB,
  output [1:0] W_op,
  output MemWrite,
  output [1:0] Dinop,
  output ERET,
  output RT,
  output RS
);

  wire and_1_out, and_2_out, and_3_out, and_4_out, and_5_out, and_6_out, and_7_out, and_8_out, and_9_out,
       and_10_out, and_11_out, and_12_out, and_13_out, and_14_out, and_15_out, and_16_out, and_17_out,
       and_18_out, and_19_out, and_20_out, and_21_out, and_22_out, and_23_out, and_24_out, and_25_out,
       and_26_out, and_27_out, and_28_out, and_29_out, and_30_out, and_31_out, and_32_out, and_33_out,
       and_34_out, and_35_out, and_36_out, and_38_out, and_39_out, and_41_out, and_42_out, and_43_out,
       and_44_out, and_45_out, and_46_out, and_47_out, and_48_out, and_49_out, and_50_out, and_51_out,
       and_52_out, and_53_out, and_54_out, and_55_out, and_56_out, and_57_out, and_60_out, and_61_out,
       and_62_out, and_63_out, and_64_out, and_65_out, and_66_out, and_67_out, and_68_out, and_69_out,
       and_70_out, and_71_out, and_72_out, and_73_out, and_74_out, and_75_out, not_1_out, not_2_out,
       not_3_out, not_4_out, not_5_out, not_6_out, not_7_out, not_8_out, not_9_out, not_10_out, not_11_out,
       not_12_out, not_13_out, not_14_out, not_15_out, not_16_out, not_17_out, not_18_out, not_19_out,
       not_20_out, not_21_out, not_22_out, not_23_out, not_24_out, not_25_out, not_26_out, not_27_out,
       not_28_out, not_29_out, not_30_out, not_31_out, not_32_out, not_33_out, not_34_out, not_35_out,
       not_36_out, not_37_out, not_38_out, not_39_out, not_40_out, not_41_out, not_42_out, not_43_out,
       not_44_out, not_45_out, not_46_out, not_47_out, not_48_out, not_49_out, not_50_out, not_51_out,
       not_52_out, not_53_out, not_54_out, not_55_out, not_56_out, not_57_out, not_58_out, not_59_out,
       not_60_out, not_61_out, not_62_out, not_63_out, not_64_out, not_65_out, not_66_out, not_67_out,
       not_68_out, not_69_out, not_70_out, not_71_out, not_72_out, not_73_out, not_74_out, not_75_out,
       not_76_out, not_77_out, not_78_out, not_79_out, not_80_out, not_81_out, not_82_out, not_83_out,
       not_84_out, not_85_out, not_86_out, not_87_out, not_88_out, not_89_out, not_90_out, not_91_out,
       not_92_out, not_93_out, not_94_out, not_95_out, not_96_out, not_97_out, not_98_out, not_99_out,
       not_100_out, not_101_out, not_102_out, not_103_out, not_104_out, not_105_out, not_106_out,
       not_107_out, not_108_out, not_109_out, not_110_out, not_111_out, not_112_out, not_113_out,
       not_114_out, not_115_out, not_116_out, not_117_out, not_118_out, not_119_out, not_120_out,
       not_121_out, not_122_out, not_123_out, not_124_out, not_125_out, not_126_out, not_127_out,
       not_128_out, not_129_out, not_130_out, not_131_out, not_132_out, not_133_out, not_134_out,
       not_135_out, not_136_out, not_137_out, not_138_out, not_139_out, not_140_out, not_141_out,
       not_142_out, not_143_out, not_144_out, not_145_out, not_146_out, not_147_out, not_148_out,
       not_149_out, not_150_out, not_151_out, not_152_out, not_153_out, not_154_out, not_155_out,
       not_156_out, not_157_out, not_158_out, not_159_out, not_160_out, not_161_out, not_162_out,
       not_163_out, not_164_out, not_165_out, not_166_out, not_167_out, not_168_out, not_169_out,
       not_170_out, not_171_out, not_172_out, not_173_out, not_174_out, not_175_out, not_176_out,
       not_177_out, not_178_out, not_179_out, not_180_out, not_181_out, not_182_out, not_183_out,
       not_184_out, not_185_out, not_186_out, not_187_out, not_188_out, not_189_out, not_190_out,
       not_191_out, not_192_out, not_193_out, not_194_out, not_195_out, not_196_out, not_197_out,
       not_198_out, not_199_out, not_200_out, not_201_out, not_202_out, not_203_out, not_204_out,
       not_205_out, not_206_out, not_207_out, not_208_out, not_209_out, not_210_out, not_211_out,
       not_212_out, not_213_out, not_214_out, not_215_out, not_216_out, not_217_out, not_218_out,
       not_219_out, not_220_out, not_221_out, not_222_out, not_223_out, not_224_out, not_225_out,
       not_226_out, not_227_out, not_228_out, not_229_out, not_230_out, not_231_out, not_232_out,
       not_233_out, not_234_out, not_235_out, not_236_out, not_237_out, not_238_out, not_239_out,
       not_240_out, not_241_out, not_242_out, not_243_out, not_244_out, not_245_out, not_246_out,
       not_247_out, not_248_out, not_249_out, not_250_out, not_251_out, not_252_out, not_253_out,
       not_254_out, not_255_out, not_256_out, not_257_out, not_258_out, not_259_out, not_260_out,
       not_261_out, not_262_out, not_263_out, not_264_out, not_265_out, not_266_out, not_267_out,
       not_268_out, not_269_out, not_270_out, not_271_out, not_272_out, not_273_out, not_274_out,
       not_275_out, not_276_out, not_277_out, not_278_out, not_279_out, not_280_out, not_281_out,
       not_282_out, not_283_out, not_284_out, not_285_out, not_286_out, not_287_out, not_288_out,
       not_289_out, not_290_out, not_291_out, not_292_out, not_293_out, not_294_out, not_295_out,
       not_296_out, not_297_out, not_298_out, not_299_out, not_300_out, not_301_out, not_302_out,
       not_303_out, not_304_out, not_305_out, not_306_out, not_307_out, not_308_out, not_309_out,
       not_310_out, not_311_out, not_312_out, not_313_out, not_314_out, not_315_out, not_316_out,
       not_317_out, not_318_out, not_319_out, not_320_out, not_321_out, not_322_out, not_323_out,
       not_324_out, not_325_out, not_326_out, not_327_out, not_328_out, not_329_out, not_330_out,
       not_331_out, not_332_out, not_333_out, not_334_out, not_335_out, not_336_out, not_337_out,
       not_338_out, not_339_out, not_340_out, not_341_out, not_342_out, not_343_out, not_344_out,
       not_345_out, not_346_out, not_347_out, not_348_out, not_349_out, not_350_out, not_351_out,
       not_352_out, not_353_out, not_354_out, not_355_out, not_356_out, not_357_out, not_358_out,
       not_359_out, not_360_out, not_361_out, not_362_out, not_363_out, not_364_out, not_365_out,
       not_366_out, not_367_out, not_368_out, not_369_out, not_370_out, not_371_out, not_372_out,
       not_373_out, not_374_out, not_375_out, not_376_out, not_377_out, not_378_out, not_379_out,
       not_380_out, not_381_out, not_382_out, not_383_out, not_384_out, not_385_out, not_386_out,
       not_387_out, not_388_out, not_389_out, not_390_out, not_391_out, not_392_out, not_393_out,
       not_394_out, not_395_out, not_396_out, not_397_out, not_398_out, not_399_out, not_400_out,
       not_401_out, not_402_out, not_403_out, not_404_out, not_405_out, not_406_out, not_407_out,
       not_408_out, not_409_out, not_410_out, not_411_out, not_412_out, not_413_out, not_414_out,
       not_415_out, not_416_out, not_417_out, not_418_out, not_419_out, not_420_out, not_421_out,
       not_422_out, not_423_out, not_424_out, not_425_out, not_426_out, not_427_out, not_428_out,
       not_429_out, not_430_out, not_431_out, not_432_out, not_433_out, not_434_out, not_435_out,
       not_436_out, not_437_out, not_438_out, not_439_out, not_440_out, not_441_out, not_442_out,
       not_443_out, not_444_out, not_445_out, not_446_out, not_447_out, not_448_out, not_449_out,
       not_450_out, not_451_out, not_452_out, not_453_out, not_454_out, not_455_out, not_456_out,
       not_457_out, not_458_out, not_459_out, not_460_out, not_461_out, not_462_out, not_463_out,
       not_464_out, not_465_out, not_466_out, not_467_out, not_468_out, not_469_out, not_470_out,
       not_471_out, not_472_out, not_473_out, not_474_out, not_475_out, not_476_out, not_477_out,
       not_478_out, not_479_out, not_480_out, not_481_out, not_482_out, or_5_out, or_13_out;

  not not_1 (not_1_out, op[5]);
  not not_2 (not_2_out, op[4]);
  not not_3 (not_3_out, op[3]);
  not not_4 (not_4_out, op[2]);
  not not_5 (not_5_out, op[1]);
  not not_6 (not_6_out, op[0]);
  not not_7 (not_7_out, fun[4]);
  not not_8 (not_8_out, fun[3]);
  not not_9 (not_9_out, op[5]);
  not not_10 (not_10_out, op[4]);
  not not_11 (not_11_out, op[3]);
  not not_12 (not_12_out, op[2]);
  not not_13 (not_13_out, op[1]);
  not not_14 (not_14_out, op[0]);
  not not_15 (not_15_out, fun[4]);
  not not_16 (not_16_out, fun[2]);
  not not_17 (not_17_out, op[5]);
  not not_18 (not_18_out, op[4]);
  not not_19 (not_19_out, op[2]);
  not not_20 (not_20_out, op[0]);
  not not_21 (not_21_out, op[5]);
  not not_22 (not_22_out, op[4]);
  not not_23 (not_23_out, op[1]);
  not not_24 (not_24_out, op[5]);
  not not_25 (not_25_out, op[4]);
  not not_26 (not_26_out, op[2]);
  not not_27 (not_27_out, op[1]);
  not not_28 (not_28_out, op[0]);
  not not_29 (not_29_out, fun[4]);
  not not_30 (not_30_out, fun[3]);
  not not_31 (not_31_out, fun[2]);
  not not_32 (not_32_out, fun[1]);
  not not_33 (not_33_out, op[5]);
  not not_34 (not_34_out, op[4]);
  not not_35 (not_35_out, op[2]);
  not not_36 (not_36_out, op[1]);
  not not_37 (not_37_out, op[0]);
  not not_38 (not_38_out, fun[4]);
  not not_39 (not_39_out, fun[3]);
  not not_40 (not_40_out, fun[2]);
  not not_41 (not_41_out, fun[0]);
  not not_42 (not_42_out, op[5]);
  not not_43 (not_43_out, op[4]);
  not not_44 (not_44_out, op[2]);
  not not_45 (not_45_out, op[1]);
  not not_46 (not_46_out, op[0]);
  not not_47 (not_47_out, fun[4]);
  not not_48 (not_48_out, fun[3]);
  not not_49 (not_49_out, fun[1]);
  not not_50 (not_50_out, fun[0]);
  not not_51 (not_51_out, op[5]);
  not not_52 (not_52_out, op[4]);
  not not_53 (not_53_out, op[2]);
  not not_54 (not_54_out, op[1]);
  not not_55 (not_55_out, op[0]);
  not not_56 (not_56_out, fun[4]);
  not not_57 (not_57_out, fun[2]);
  not not_58 (not_58_out, op[5]);
  not not_59 (not_59_out, op[4]);
  not not_60 (not_60_out, op[2]);
  not not_61 (not_61_out, op[1]);
  not not_62 (not_62_out, op[5]);
  not not_63 (not_63_out, op[4]);
  not not_64 (not_64_out, op[1]);
  not not_65 (not_65_out, op[0]);
  not not_66 (not_66_out, op[4]);
  not not_67 (not_67_out, op[2]);
  and and_1 (and_1_out, not_1_out, not_2_out, not_3_out, not_4_out, not_5_out, not_6_out, fun[5], not_7_out, not_8_out, fun[2], fun[0]);
  and and_2 (and_2_out, not_9_out, not_10_out, not_11_out, not_12_out, not_13_out, not_14_out, fun[5], not_15_out, fun[3], not_16_out, fun[1]);
  and and_3 (and_3_out, not_17_out, not_18_out, op[3], not_19_out, op[1], not_20_out);
  and and_4 (and_4_out, not_21_out, not_22_out, op[3], op[2], not_23_out, op[0]);
  and and_5 (and_5_out, not_24_out, not_25_out, not_26_out, not_27_out, not_28_out, fun[5], not_29_out, not_30_out, not_31_out, not_32_out);
  and and_6 (and_6_out, not_33_out, not_34_out, not_35_out, not_36_out, not_37_out, fun[5], not_38_out, not_39_out, not_40_out, not_41_out);
  and and_7 (and_7_out, not_42_out, not_43_out, not_44_out, not_45_out, not_46_out, fun[5], not_47_out, not_48_out, not_49_out, not_50_out);
  and and_8 (and_8_out, not_51_out, not_52_out, not_53_out, not_54_out, not_55_out, fun[5], not_56_out, fun[3], not_57_out, fun[1], fun[0]);
  and and_9 (and_9_out, not_58_out, not_59_out, op[3], not_60_out, not_61_out);
  and and_10 (and_10_out, not_62_out, not_63_out, op[3], not_64_out, not_65_out);
  and and_11 (and_11_out, op[5], not_66_out, not_67_out, op[1], op[0]);
  or or_1 (ALUop[3], and_1_out, and_2_out, and_3_out, and_4_out);
  or or_2 (ALUop[2], and_5_out, and_6_out, and_7_out, and_8_out, and_9_out, and_10_out, and_11_out);
  not not_68 (not_68_out, op[5]);
  not not_69 (not_69_out, op[4]);
  not not_70 (not_70_out, op[3]);
  not not_71 (not_71_out, op[2]);
  not not_72 (not_72_out, op[1]);
  not not_73 (not_73_out, op[0]);
  not not_74 (not_74_out, fun[4]);
  not not_75 (not_75_out, fun[3]);
  not not_76 (not_76_out, fun[2]);
  not not_77 (not_77_out, fun[0]);
  not not_78 (not_78_out, op[5]);
  not not_79 (not_79_out, op[4]);
  not not_80 (not_80_out, op[3]);
  not not_81 (not_81_out, op[2]);
  not not_82 (not_82_out, op[1]);
  not not_83 (not_83_out, op[0]);
  not not_84 (not_84_out, fun[4]);
  not not_85 (not_85_out, fun[2]);
  not not_86 (not_86_out, fun[0]);
  not not_87 (not_87_out, op[5]);
  not not_88 (not_88_out, op[4]);
  not not_89 (not_89_out, op[3]);
  not not_90 (not_90_out, op[2]);
  not not_91 (not_91_out, op[1]);
  not not_92 (not_92_out, op[0]);
  not not_93 (not_93_out, fun[4]);
  not not_94 (not_94_out, fun[3]);
  not not_95 (not_95_out, fun[1]);
  not not_96 (not_96_out, fun[0]);
  not not_97 (not_97_out, op[5]);
  not not_98 (not_98_out, op[4]);
  not not_99 (not_99_out, op[3]);
  not not_100 (not_100_out, op[2]);
  not not_101 (not_101_out, op[1]);
  not not_102 (not_102_out, op[0]);
  not not_103 (not_103_out, fun[4]);
  not not_104 (not_104_out, fun[3]);
  not not_105 (not_105_out, op[5]);
  not not_106 (not_106_out, op[4]);
  not not_107 (not_107_out, op[2]);
  not not_108 (not_108_out, op[0]);
  not not_109 (not_109_out, op[5]);
  not not_110 (not_110_out, op[4]);
  not not_111 (not_111_out, op[1]);
  not not_112 (not_112_out, op[0]);
  not not_113 (not_113_out, op[5]);
  not not_114 (not_114_out, op[4]);
  not not_115 (not_115_out, op[2]);
  not not_116 (not_116_out, op[1]);
  not not_117 (not_117_out, op[0]);
  not not_118 (not_118_out, fun[5]);
  not not_119 (not_119_out, fun[4]);
  not not_120 (not_120_out, fun[3]);
  not not_121 (not_121_out, fun[2]);
  not not_122 (not_122_out, op[5]);
  not not_123 (not_123_out, op[4]);
  not not_124 (not_124_out, op[2]);
  not not_125 (not_125_out, op[1]);
  not not_126 (not_126_out, op[0]);
  not not_127 (not_127_out, fun[4]);
  not not_128 (not_128_out, fun[3]);
  not not_129 (not_129_out, fun[2]);
  not not_130 (not_130_out, fun[1]);
  not not_131 (not_131_out, op[5]);
  not not_132 (not_132_out, op[4]);
  not not_133 (not_133_out, op[2]);
  not not_134 (not_134_out, op[1]);
  not not_135 (not_135_out, op[0]);
  not not_136 (not_136_out, fun[4]);
  not not_137 (not_137_out, fun[3]);
  not not_138 (not_138_out, fun[1]);
  not not_139 (not_139_out, fun[0]);
  not not_140 (not_140_out, op[5]);
  not not_141 (not_141_out, op[4]);
  not not_142 (not_142_out, op[2]);
  not not_143 (not_143_out, op[1]);
  not not_144 (not_144_out, op[0]);
  not not_145 (not_145_out, fun[4]);
  not not_146 (not_146_out, fun[2]);
  not not_147 (not_147_out, fun[0]);
  not not_148 (not_148_out, op[5]);
  not not_149 (not_149_out, op[4]);
  not not_150 (not_150_out, op[2]);
  not not_151 (not_151_out, op[1]);
  not not_152 (not_152_out, op[5]);
  not not_153 (not_153_out, op[4]);
  not not_154 (not_154_out, op[2]);
  not not_155 (not_155_out, op[0]);
  not not_156 (not_156_out, op[5]);
  not not_157 (not_157_out, op[4]);
  not not_158 (not_158_out, op[1]);
  not not_159 (not_159_out, op[0]);
  not not_160 (not_160_out, op[4]);
  not not_161 (not_161_out, op[2]);
  and and_12 (and_12_out, not_68_out, not_69_out, not_70_out, not_71_out, not_72_out, not_73_out, not_74_out, not_75_out, not_76_out, fun[1], not_77_out);
  and and_13 (and_13_out, not_78_out, not_79_out, not_80_out, not_81_out, not_82_out, not_83_out, fun[5], not_84_out, not_85_out, fun[1], not_86_out);
  and and_14 (and_14_out, not_87_out, not_88_out, not_89_out, not_90_out, not_91_out, not_92_out, fun[5], not_93_out, not_94_out, fun[2], not_95_out, not_96_out);
  and and_15 (and_15_out, not_97_out, not_98_out, not_99_out, not_100_out, not_101_out, not_102_out, fun[5], not_103_out, not_104_out, fun[2], fun[1], fun[0]);
  and and_16 (and_16_out, not_105_out, not_106_out, op[3], not_107_out, op[1], not_108_out);
  and and_17 (and_17_out, not_109_out, not_110_out, op[3], op[2], not_111_out, not_112_out);
  and and_18 (and_18_out, not_113_out, not_114_out, not_115_out, not_116_out, not_117_out, not_118_out, not_119_out, not_120_out, not_121_out, fun[1], fun[0]);
  and and_19 (and_19_out, not_122_out, not_123_out, not_124_out, not_125_out, not_126_out, fun[5], not_127_out, not_128_out, not_129_out, not_130_out);
  and and_20 (and_20_out, not_131_out, not_132_out, not_133_out, not_134_out, not_135_out, fun[5], not_136_out, not_137_out, not_138_out, not_139_out);
  and and_21 (and_21_out, not_140_out, not_141_out, not_142_out, not_143_out, not_144_out, fun[5], not_145_out, fun[3], not_146_out, fun[1], not_147_out);
  and and_22 (and_22_out, not_148_out, not_149_out, op[3], not_150_out, not_151_out);
  and and_23 (and_23_out, not_152_out, not_153_out, op[3], not_154_out, not_155_out);
  and and_24 (and_24_out, not_156_out, not_157_out, op[3], not_158_out, not_159_out);
  and and_25 (and_25_out, op[5], not_160_out, not_161_out, op[1], op[0]);
  or or_3 (ALUop[1], and_12_out, and_13_out, and_14_out, and_15_out, and_16_out, and_17_out);
  or or_4 (ALUop[0], and_18_out, and_19_out, and_20_out, and_21_out, and_22_out, and_23_out, and_24_out, and_25_out);
  not not_162 (not_162_out, op[5]);
  not not_163 (not_163_out, op[4]);
  not not_164 (not_164_out, op[3]);
  not not_165 (not_165_out, op[2]);
  not not_166 (not_166_out, op[0]);
  not not_167 (not_167_out, fun[5]);
  not not_168 (not_168_out, fun[4]);
  not not_169 (not_169_out, fun[2]);
  not not_170 (not_170_out, fun[1]);
  not not_171 (not_171_out, fun[0]);
  not not_172 (not_172_out, op[5]);
  not not_173 (not_173_out, op[4]);
  not not_174 (not_174_out, op[3]);
  not not_175 (not_175_out, op[2]);
  not not_176 (not_176_out, op[5]);
  not not_177 (not_177_out, op[4]);
  not not_178 (not_178_out, op[2]);
  not not_179 (not_179_out, op[0]);
  not not_180 (not_180_out, op[5]);
  not not_181 (not_181_out, op[4]);
  not not_182 (not_182_out, op[1]);
  not not_183 (not_183_out, op[4]);
  not not_184 (not_184_out, op[3]);
  not not_185 (not_185_out, op[2]);
  not not_186 (not_186_out, op[5]);
  not not_187 (not_187_out, op[3]);
  not not_188 (not_188_out, op[2]);
  not not_189 (not_189_out, op[1]);
  not not_190 (not_190_out, op[0]);
  not not_191 (not_191_out, M[4]);
  not not_192 (not_192_out, M[3]);
  not not_193 (not_193_out, M[2]);
  not not_194 (not_194_out, M[1]);
  not not_195 (not_195_out, M[0]);
  not not_196 (not_196_out, op[5]);
  not not_197 (not_197_out, op[4]);
  not not_198 (not_198_out, op[3]);
  not not_199 (not_199_out, op[2]);
  not not_200 (not_200_out, op[1]);
  not not_201 (not_201_out, op[0]);
  not not_202 (not_202_out, fun[5]);
  not not_203 (not_203_out, fun[4]);
  not not_204 (not_204_out, fun[3]);
  not not_205 (not_205_out, fun[2]);
  not not_206 (not_206_out, fun[0]);
  not not_207 (not_207_out, op[5]);
  not not_208 (not_208_out, op[4]);
  not not_209 (not_209_out, op[3]);
  not not_210 (not_210_out, op[2]);
  not not_211 (not_211_out, op[1]);
  not not_212 (not_212_out, op[0]);
  not not_213 (not_213_out, fun[5]);
  not not_214 (not_214_out, fun[4]);
  not not_215 (not_215_out, fun[3]);
  not not_216 (not_216_out, fun[2]);
  not not_217 (not_217_out, op[5]);
  not not_218 (not_218_out, op[4]);
  not not_219 (not_219_out, op[3]);
  not not_220 (not_220_out, op[2]);
  not not_221 (not_221_out, op[1]);
  not not_222 (not_222_out, op[0]);
  not not_223 (not_223_out, fun[5]);
  not not_224 (not_224_out, fun[4]);
  not not_225 (not_225_out, fun[1]);
  not not_226 (not_226_out, fun[0]);
  and and_26 (and_26_out, not_176_out, not_177_out, op[3], not_178_out, not_179_out);
  and and_27 (and_27_out, not_180_out, not_181_out, op[3], not_182_out);
  and and_28 (and_28_out, op[5], not_183_out, not_184_out, not_185_out, op[1], op[0]);
  not not_227 (not_227_out, op[4]);
  not not_228 (not_228_out, op[3]);
  not not_229 (not_229_out, op[2]);
  not not_230 (not_230_out, op[5]);
  not not_231 (not_231_out, op[3]);
  not not_232 (not_232_out, op[2]);
  not not_233 (not_233_out, op[1]);
  not not_234 (not_234_out, op[0]);
  not not_235 (not_235_out, M[4]);
  not not_236 (not_236_out, M[3]);
  not not_237 (not_237_out, M[2]);
  not not_238 (not_238_out, M[1]);
  not not_239 (not_239_out, M[0]);
  not not_240 (not_240_out, op[4]);
  not not_241 (not_241_out, op[2]);
  and and_29 (and_29_out, not_162_out, not_163_out, not_164_out, not_165_out, not_166_out, not_167_out, not_168_out, fun[3], not_169_out, not_170_out, not_171_out);
  and and_30 (and_30_out, not_172_out, not_173_out, not_174_out, not_175_out, op[1]);
  or or_5 (or_5_out, and_26_out, and_27_out, and_28_out);
  and and_31 (and_31_out, not_186_out, op[4], not_187_out, not_188_out, not_189_out, not_190_out, not_191_out, not_192_out, not_193_out, not_194_out, not_195_out);
  and and_32 (and_32_out, op[5], not_227_out, not_228_out, not_229_out, op[1], op[0]);
  and and_33 (and_33_out, not_230_out, op[4], not_231_out, not_232_out, not_233_out, not_234_out, not_235_out, not_236_out, not_237_out, not_238_out, not_239_out);
  and and_34 (and_34_out, not_196_out, not_197_out, not_198_out, not_199_out, not_200_out, not_201_out, not_202_out, not_203_out, not_204_out, not_205_out, not_206_out);
  and and_35 (and_35_out, not_207_out, not_208_out, not_209_out, not_210_out, not_211_out, not_212_out, not_213_out, not_214_out, not_215_out, not_216_out, fun[1]);
  and and_36 (and_36_out, not_217_out, not_218_out, not_219_out, not_220_out, not_221_out, not_222_out, not_223_out, not_224_out, fun[3], fun[2], not_225_out, not_226_out);
  and and_37 (MemWrite, op[5], not_240_out, op[3], not_241_out, op[1], op[0]);
  or or_6 (PCop[1], and_29_out, and_30_out);
  or or_7 (W_op[1], or_5_out, and_31_out);
  or or_8 (Dinop[1], and_32_out, and_33_out);
  or or_9 (AluScrA, and_34_out, and_35_out, and_36_out);
  not not_242 (not_242_out, op[5]);
  not not_243 (not_243_out, op[4]);
  not not_244 (not_244_out, op[3]);
  not not_245 (not_245_out, op[1]);
  not not_246 (not_246_out, op[0]);
  not not_247 (not_247_out, fun[5]);
  not not_248 (not_248_out, fun[4]);
  not not_249 (not_249_out, fun[2]);
  not not_250 (not_250_out, fun[1]);
  not not_251 (not_251_out, fun[0]);
  not not_252 (not_252_out, op[5]);
  not not_253 (not_253_out, op[4]);
  not not_254 (not_254_out, op[3]);
  not not_255 (not_255_out, op[1]);
  not not_256 (not_256_out, op[5]);
  not not_257 (not_257_out, op[4]);
  not not_258 (not_258_out, op[3]);
  not not_259 (not_259_out, op[2]);
  not not_260 (not_260_out, op[5]);
  not not_261 (not_261_out, op[4]);
  not not_262 (not_262_out, op[2]);
  not not_263 (not_263_out, op[0]);
  not not_264 (not_264_out, op[4]);
  not not_265 (not_265_out, op[2]);
  not not_266 (not_266_out, op[5]);
  not not_267 (not_267_out, op[4]);
  not not_268 (not_268_out, op[3]);
  not not_269 (not_269_out, op[1]);
  not not_270 (not_270_out, op[0]);
  not not_271 (not_271_out, fun[5]);
  not not_272 (not_272_out, fun[4]);
  not not_273 (not_273_out, fun[1]);
  not not_274 (not_274_out, fun[0]);
  not not_275 (not_275_out, op[5]);
  not not_276 (not_276_out, op[4]);
  not not_277 (not_277_out, op[3]);
  not not_278 (not_278_out, op[1]);
  not not_279 (not_279_out, op[0]);
  not not_280 (not_280_out, fun[4]);
  not not_281 (not_281_out, fun[3]);
  not not_282 (not_282_out, fun[2]);
  not not_283 (not_283_out, fun[0]);
  not not_284 (not_284_out, op[5]);
  not not_285 (not_285_out, op[4]);
  not not_286 (not_286_out, op[3]);
  not not_287 (not_287_out, op[1]);
  not not_288 (not_288_out, op[0]);
  not not_289 (not_289_out, fun[4]);
  not not_290 (not_290_out, fun[3]);
  not not_291 (not_291_out, fun[1]);
  not not_292 (not_292_out, op[5]);
  not not_293 (not_293_out, op[4]);
  not not_294 (not_294_out, op[3]);
  not not_295 (not_295_out, op[1]);
  not not_296 (not_296_out, op[0]);
  not not_297 (not_297_out, fun[4]);
  not not_298 (not_298_out, fun[3]);
  not not_299 (not_299_out, op[5]);
  not not_300 (not_300_out, op[4]);
  not not_301 (not_301_out, op[3]);
  not not_302 (not_302_out, op[1]);
  not not_303 (not_303_out, op[0]);
  not not_304 (not_304_out, fun[4]);
  not not_305 (not_305_out, fun[2]);
  not not_306 (not_306_out, op[5]);
  not not_307 (not_307_out, op[4]);
  not not_308 (not_308_out, op[3]);
  not not_309 (not_309_out, op[1]);
  and and_38 (and_38_out, not_242_out, not_243_out, not_244_out, not_245_out, not_246_out, not_247_out, not_248_out, fun[3], not_249_out, not_250_out, not_251_out);
  and and_39 (and_39_out, not_252_out, not_253_out, not_254_out, op[2], not_255_out);
  and and_40 (Dinop[0], not_256_out, not_257_out, not_258_out, not_259_out, op[1], op[0]);
  and and_41 (and_41_out, not_260_out, not_261_out, op[3], not_262_out, not_263_out);
  and and_42 (and_42_out, op[5], not_264_out, not_265_out, op[1], op[0]);
  and and_43 (and_43_out, not_266_out, not_267_out, not_268_out, not_269_out, not_270_out, not_271_out, not_272_out, fun[3], fun[2], not_273_out, not_274_out);
  and and_44 (and_44_out, not_275_out, not_276_out, not_277_out, not_278_out, not_279_out, fun[5], not_280_out, not_281_out, not_282_out, not_283_out);
  and and_45 (and_45_out, not_284_out, not_285_out, not_286_out, not_287_out, not_288_out, fun[5], not_289_out, not_290_out, not_291_out);
  and and_46 (and_46_out, not_292_out, not_293_out, not_294_out, not_295_out, not_296_out, fun[5], not_297_out, not_298_out, fun[2], fun[0]);
  and and_47 (and_47_out, not_299_out, not_300_out, not_301_out, not_302_out, not_303_out, fun[5], not_304_out, fun[3], not_305_out, fun[1]);
  and and_48 (and_48_out, not_306_out, not_307_out, not_308_out, op[2], not_309_out);
  or or_10 (PCop[0], and_38_out, and_39_out);
  or or_11 (SingnedIMM, and_41_out, and_42_out);
  or or_12 (AluSrcB[1], and_43_out, and_44_out, and_45_out, and_46_out, and_47_out, and_48_out);
  not not_310 (not_310_out, op[5]);
  not not_311 (not_311_out, op[4]);
  not not_312 (not_312_out, op[2]);
  not not_313 (not_313_out, op[1]);
  not not_314 (not_314_out, op[0]);
  not not_315 (not_315_out, fun[4]);
  not not_316 (not_316_out, fun[3]);
  not not_317 (not_317_out, fun[2]);
  not not_318 (not_318_out, fun[0]);
  not not_319 (not_319_out, op[5]);
  not not_320 (not_320_out, op[4]);
  not not_321 (not_321_out, op[2]);
  not not_322 (not_322_out, op[1]);
  not not_323 (not_323_out, op[0]);
  not not_324 (not_324_out, fun[5]);
  not not_325 (not_325_out, fun[4]);
  not not_326 (not_326_out, fun[3]);
  not not_327 (not_327_out, fun[2]);
  not not_328 (not_328_out, op[5]);
  not not_329 (not_329_out, op[4]);
  not not_330 (not_330_out, op[2]);
  not not_331 (not_331_out, op[1]);
  not not_332 (not_332_out, op[0]);
  not not_333 (not_333_out, fun[4]);
  not not_334 (not_334_out, fun[3]);
  not not_335 (not_335_out, fun[1]);
  not not_336 (not_336_out, op[5]);
  not not_337 (not_337_out, op[4]);
  not not_338 (not_338_out, op[2]);
  not not_339 (not_339_out, op[1]);
  not not_340 (not_340_out, op[0]);
  not not_341 (not_341_out, fun[4]);
  not not_342 (not_342_out, fun[3]);
  not not_343 (not_343_out, op[5]);
  not not_344 (not_344_out, op[4]);
  not not_345 (not_345_out, op[2]);
  not not_346 (not_346_out, op[1]);
  not not_347 (not_347_out, op[0]);
  not not_348 (not_348_out, fun[4]);
  not not_349 (not_349_out, fun[2]);
  not not_350 (not_350_out, op[4]);
  not not_351 (not_351_out, op[3]);
  not not_352 (not_352_out, op[2]);
  not not_353 (not_353_out, op[5]);
  not not_354 (not_354_out, op[4]);
  not not_355 (not_355_out, op[2]);
  not not_356 (not_356_out, op[0]);
  not not_357 (not_357_out, op[5]);
  not not_358 (not_358_out, op[4]);
  not not_359 (not_359_out, op[1]);
  not not_360 (not_360_out, op[5]);
  not not_361 (not_361_out, op[3]);
  not not_362 (not_362_out, op[2]);
  not not_363 (not_363_out, op[1]);
  not not_364 (not_364_out, op[0]);
  not not_365 (not_365_out, M[4]);
  not not_366 (not_366_out, M[3]);
  not not_367 (not_367_out, M[2]);
  not not_368 (not_368_out, M[1]);
  not not_369 (not_369_out, M[0]);
  and and_49 (and_49_out, not_310_out, not_311_out, not_312_out, not_313_out, not_314_out, not_315_out, not_316_out, not_317_out, not_318_out);
  and and_50 (and_50_out, not_319_out, not_320_out, not_321_out, not_322_out, not_323_out, not_324_out, not_325_out, not_326_out, not_327_out, fun[1]);
  and and_51 (and_51_out, not_328_out, not_329_out, not_330_out, not_331_out, not_332_out, fun[5], not_333_out, not_334_out, not_335_out);
  and and_52 (and_52_out, not_336_out, not_337_out, not_338_out, not_339_out, not_340_out, fun[5], not_341_out, not_342_out, fun[2], fun[0]);
  and and_53 (and_53_out, not_343_out, not_344_out, not_345_out, not_346_out, not_347_out, fun[5], not_348_out, fun[3], not_349_out, fun[1]);
  and and_54 (and_54_out, not_350_out, not_351_out, not_352_out, op[1], op[0]);
  and and_55 (and_55_out, not_353_out, not_354_out, op[3], not_355_out, not_356_out);
  and and_56 (and_56_out, not_357_out, not_358_out, op[3], not_359_out);
  and and_57 (and_57_out, not_360_out, op[4], not_361_out, not_362_out, not_363_out, not_364_out, not_365_out, not_366_out, not_367_out, not_368_out, not_369_out);
  or or_13 (or_13_out, and_49_out, and_50_out, and_51_out, and_52_out, and_53_out, and_54_out, and_55_out, and_56_out);
  or or_14 (RegWrite, or_13_out, and_57_out);
  not not_370 (not_370_out, op[5]);
  not not_371 (not_371_out, op[4]);
  not not_372 (not_372_out, op[3]);
  not not_373 (not_373_out, op[2]);
  not not_374 (not_374_out, op[1]);
  not not_375 (not_375_out, op[0]);
  not not_376 (not_376_out, fun[5]);
  not not_377 (not_377_out, fun[4]);
  not not_378 (not_378_out, fun[1]);
  not not_379 (not_379_out, fun[0]);
  not not_380 (not_380_out, op[5]);
  not not_381 (not_381_out, op[3]);
  not not_382 (not_382_out, op[2]);
  not not_383 (not_383_out, op[1]);
  not not_384 (not_384_out, op[0]);
  not not_385 (not_385_out, M[3]);
  not not_386 (not_386_out, M[2]);
  not not_387 (not_387_out, M[1]);
  not not_388 (not_388_out, M[0]);
  not not_389 (not_389_out, op[5]);
  not not_390 (not_390_out, op[4]);
  not not_391 (not_391_out, op[1]);
  not not_392 (not_392_out, op[0]);
  not not_393 (not_393_out, fun[5]);
  not not_394 (not_394_out, fun[4]);
  not not_395 (not_395_out, fun[2]);
  not not_396 (not_396_out, fun[1]);
  not not_397 (not_397_out, fun[0]);
  not not_398 (not_398_out, op[5]);
  not not_399 (not_399_out, op[4]);
  not not_400 (not_400_out, op[1]);
  not not_401 (not_401_out, op[0]);
  not not_402 (not_402_out, fun[4]);
  not not_403 (not_403_out, fun[3]);
  not not_404 (not_404_out, fun[2]);
  not not_405 (not_405_out, fun[0]);
  not not_406 (not_406_out, op[5]);
  not not_407 (not_407_out, op[4]);
  not not_408 (not_408_out, op[1]);
  not not_409 (not_409_out, op[0]);
  not not_410 (not_410_out, fun[4]);
  not not_411 (not_411_out, fun[3]);
  not not_412 (not_412_out, fun[1]);
  not not_413 (not_413_out, op[5]);
  not not_414 (not_414_out, op[4]);
  not not_415 (not_415_out, op[1]);
  not not_416 (not_416_out, op[0]);
  not not_417 (not_417_out, fun[4]);
  not not_418 (not_418_out, fun[3]);
  not not_419 (not_419_out, op[5]);
  not not_420 (not_420_out, op[4]);
  not not_421 (not_421_out, op[1]);
  not not_422 (not_422_out, op[0]);
  not not_423 (not_423_out, fun[4]);
  not not_424 (not_424_out, fun[2]);
  not not_425 (not_425_out, op[5]);
  not not_426 (not_426_out, op[4]);
  not not_427 (not_427_out, op[1]);
  not not_428 (not_428_out, op[5]);
  not not_429 (not_429_out, op[4]);
  not not_430 (not_430_out, op[2]);
  not not_431 (not_431_out, op[0]);
  not not_432 (not_432_out, op[5]);
  not not_433 (not_433_out, op[4]);
  not not_434 (not_434_out, op[1]);
  not not_435 (not_435_out, op[4]);
  not not_436 (not_436_out, op[2]);
  and and_58 (Syscall, not_370_out, not_371_out, not_372_out, not_373_out, not_374_out, not_375_out, not_376_out, not_377_out, fun[3], fun[2], not_378_out, not_379_out);
  and and_59 (ERET, not_380_out, op[4], not_381_out, not_382_out, not_383_out, not_384_out, M[4], not_385_out, not_386_out, not_387_out, not_388_out);
  and and_60 (and_60_out, not_389_out, not_390_out, not_391_out, not_392_out, not_393_out, not_394_out, fun[3], not_395_out, not_396_out, not_397_out);
  and and_61 (and_61_out, not_398_out, not_399_out, not_400_out, not_401_out, fun[5], not_402_out, not_403_out, not_404_out, not_405_out);
  and and_62 (and_62_out, not_406_out, not_407_out, not_408_out, not_409_out, fun[5], not_410_out, not_411_out, not_412_out);
  and and_63 (and_63_out, not_413_out, not_414_out, not_415_out, not_416_out, fun[5], not_417_out, not_418_out, fun[2], fun[0]);
  and and_64 (and_64_out, not_419_out, not_420_out, not_421_out, not_422_out, fun[5], not_423_out, fun[3], not_424_out, fun[1]);
  and and_65 (and_65_out, not_425_out, not_426_out, op[2], not_427_out);
  and and_66 (and_66_out, not_428_out, not_429_out, op[3], not_430_out, not_431_out);
  and and_67 (and_67_out, not_432_out, not_433_out, op[3], not_434_out);
  and and_68 (and_68_out, op[5], not_435_out, not_436_out, op[1], op[0]);
  or or_15 (RS, and_60_out, and_61_out, and_62_out, and_63_out, and_64_out, and_65_out, and_66_out, and_67_out, and_68_out);
  not not_437 (not_437_out, op[5]);
  not not_438 (not_438_out, op[4]);
  not not_439 (not_439_out, op[3]);
  not not_440 (not_440_out, op[1]);
  not not_441 (not_441_out, op[0]);
  not not_442 (not_442_out, fun[4]);
  not not_443 (not_443_out, fun[3]);
  not not_444 (not_444_out, fun[2]);
  not not_445 (not_445_out, fun[0]);
  not not_446 (not_446_out, op[5]);
  not not_447 (not_447_out, op[4]);
  not not_448 (not_448_out, op[3]);
  not not_449 (not_449_out, op[1]);
  not not_450 (not_450_out, op[0]);
  not not_451 (not_451_out, fun[5]);
  not not_452 (not_452_out, fun[4]);
  not not_453 (not_453_out, fun[3]);
  not not_454 (not_454_out, fun[2]);
  not not_455 (not_455_out, op[5]);
  not not_456 (not_456_out, op[4]);
  not not_457 (not_457_out, op[3]);
  not not_458 (not_458_out, op[1]);
  not not_459 (not_459_out, op[0]);
  not not_460 (not_460_out, fun[4]);
  not not_461 (not_461_out, fun[3]);
  not not_462 (not_462_out, fun[1]);
  not not_463 (not_463_out, op[5]);
  not not_464 (not_464_out, op[4]);
  not not_465 (not_465_out, op[3]);
  not not_466 (not_466_out, op[1]);
  not not_467 (not_467_out, op[0]);
  not not_468 (not_468_out, fun[4]);
  not not_469 (not_469_out, fun[3]);
  not not_470 (not_470_out, op[5]);
  not not_471 (not_471_out, op[4]);
  not not_472 (not_472_out, op[3]);
  not not_473 (not_473_out, op[1]);
  not not_474 (not_474_out, op[0]);
  not not_475 (not_475_out, fun[4]);
  not not_476 (not_476_out, fun[2]);
  not not_477 (not_477_out, op[5]);
  not not_478 (not_478_out, op[4]);
  not not_479 (not_479_out, op[3]);
  not not_480 (not_480_out, op[1]);
  not not_481 (not_481_out, op[4]);
  not not_482 (not_482_out, op[2]);
  and and_69 (and_69_out, not_437_out, not_438_out, not_439_out, not_440_out, not_441_out, not_442_out, not_443_out, not_444_out, not_445_out);
  and and_70 (and_70_out, not_446_out, not_447_out, not_448_out, not_449_out, not_450_out, not_451_out, not_452_out, not_453_out, not_454_out, fun[1]);
  and and_71 (and_71_out, not_455_out, not_456_out, not_457_out, not_458_out, not_459_out, fun[5], not_460_out, not_461_out, not_462_out);
  and and_72 (and_72_out, not_463_out, not_464_out, not_465_out, not_466_out, not_467_out, fun[5], not_468_out, not_469_out, fun[2], fun[0]);
  and and_73 (and_73_out, not_470_out, not_471_out, not_472_out, not_473_out, not_474_out, fun[5], not_475_out, fun[3], not_476_out, fun[1]);
  and and_74 (and_74_out, not_477_out, not_478_out, not_479_out, op[2], not_480_out);
  and and_75 (and_75_out, op[5], not_481_out, op[3], not_482_out, op[1], op[0]);
  or or_16 (RT, and_69_out, and_70_out, and_71_out, and_72_out, and_73_out, and_74_out, and_75_out);

  assign AluSrcB[0] = AluScrA;
  assign W_op[0] = Dinop[0];

  // Other names for the same wires on the sheet: AluScrB = AluSrcB[1]; JAL = Dinop[0]; MemToReg = Dinop[1];
  //   Branch = PCop[0]; Jump = PCop[1]; RegDst = W_op[1]
endmodule

module Test (
);

  wire and_1_out, and_2_out, and_3_out, and_4_out, and_5_out, and_6_out, and_7_out, not_1_out, not_2_out,
       not_3_out, not_4_out, not_5_out, not_6_out, not_7_out, not_8_out, not_9_out, not_10_out, not_11_out,
       not_12_out, not_13_out, not_14_out, not_15_out, not_16_out, not_17_out, not_18_out, not_19_out,
       not_20_out, not_21_out, not_22_out, not_23_out, not_24_out, not_25_out, not_26_out, not_27_out,
       not_28_out, not_29_out, not_30_out, not_31_out, not_32_out, not_33_out, not_34_out, not_35_out,
       not_36_out, not_37_out, not_38_out, not_39_out, not_40_out, not_41_out, not_42_out, not_43_out,
       not_44_out, not_45_out, not_46_out, or_1_out, undriven, undriven_2, undriven_3, undriven_4,
       undriven_5, undriven_6, undriven_7, undriven_8, undriven_9, undriven_10, undriven_11, undriven_12;

  not not_1 (not_1_out, undriven);
  not not_2 (not_2_out, undriven_2);
  not not_3 (not_3_out, undriven_3);
  not not_4 (not_4_out, undriven_5);
  not not_5 (not_5_out, undriven_11);
  not not_6 (not_6_out, undriven_7);
  not not_7 (not_7_out, undriven_8);
  not not_8 (not_8_out, undriven_9);
  not not_9 (not_9_out, undriven_12);
  not not_10 (not_10_out, undriven);
  not not_11 (not_11_out, undriven_2);
  not not_12 (not_12_out, undriven_3);
  not not_13 (not_13_out, undriven_5);
  not not_14 (not_14_out, undriven_11);
  not not_15 (not_15_out, undriven_6);
  not not_16 (not_16_out, undriven_7);
  not not_17 (not_17_out, undriven_8);
  not not_18 (not_18_out, undriven_9);
  not not_19 (not_19_out, undriven);
  not not_20 (not_20_out, undriven_2);
  not not_21 (not_21_out, undriven_3);
  not not_22 (not_22_out, undriven_5);
  not not_23 (not_23_out, undriven_11);
  not not_24 (not_24_out, undriven_7);
  not not_25 (not_25_out, undriven_8);
  not not_26 (not_26_out, undriven_10);
  not not_27 (not_27_out, undriven);
  not not_28 (not_28_out, undriven_2);
  not not_29 (not_29_out, undriven_3);
  not not_30 (not_30_out, undriven_5);
  not not_31 (not_31_out, undriven_11);
  not not_32 (not_32_out, undriven_7);
  not not_33 (not_33_out, undriven_8);
  not not_34 (not_34_out, undriven);
  not not_35 (not_35_out, undriven_2);
  not not_36 (not_36_out, undriven_3);
  not not_37 (not_37_out, undriven_5);
  not not_38 (not_38_out, undriven_11);
  not not_39 (not_39_out, undriven_7);
  not not_40 (not_40_out, undriven_9);
  not not_41 (not_41_out, undriven);
  not not_42 (not_42_out, undriven_2);
  not not_43 (not_43_out, undriven_3);
  not not_44 (not_44_out, undriven_5);
  not not_45 (not_45_out, undriven_2);
  not not_46 (not_46_out, undriven_4);
  and and_1 (and_1_out, not_1_out, not_2_out, not_3_out, not_4_out, not_5_out, not_6_out, not_7_out, not_8_out, not_9_out);
  and and_2 (and_2_out, not_10_out, not_11_out, not_12_out, not_13_out, not_14_out, not_15_out, not_16_out, not_17_out, not_18_out, undriven_10);
  and and_3 (and_3_out, not_19_out, not_20_out, not_21_out, not_22_out, not_23_out, undriven_6, not_24_out, not_25_out, not_26_out);
  and and_4 (and_4_out, not_27_out, not_28_out, not_29_out, not_30_out, not_31_out, undriven_6, not_32_out, not_33_out, undriven_9, undriven_12);
  and and_5 (and_5_out, not_34_out, not_35_out, not_36_out, not_37_out, not_38_out, undriven_6, not_39_out, undriven_8, not_40_out, undriven_10);
  and and_6 (and_6_out, not_41_out, not_42_out, not_43_out, undriven_4, not_44_out);
  and and_7 (and_7_out, undriven, not_45_out, undriven_3, not_46_out, undriven_5, undriven_11);
  or or_1 (or_1_out, and_1_out, and_2_out, and_3_out, and_4_out, and_5_out, and_6_out, and_7_out);
endmodule

module Instructions (
  input  [5:0] op,
  input  clock,
  input  in_3,
  output [15:0] R_type,
  output [15:0] I_type,
  output [15:0] J_type,
  output [15:0] ALL
);

  wire and_1_out, and_2_out, and_3_out, and_4_out, and_5_out, and_6_out, not_1_out, not_2_out, not_3_out,
       not_4_out, not_5_out, not_6_out, not_7_out, not_8_out, not_9_out, not_10_out, not_11_out, not_12_out,
       not_13_out, not_14_out, not_15_out, not_16_out, not_17_out, not_18_out, not_19_out, not_20_out,
       not_21_out, not_22_out, or_1_out;
  wire [15:0] adder_1_out, adder_2_out, counter_1_q, counter_2_q;

  not not_1 (not_1_out, op[5]);
  not not_2 (not_2_out, op[4]);
  not not_3 (not_3_out, op[3]);
  not not_4 (not_4_out, op[2]);
  not not_5 (not_5_out, op[1]);
  not not_6 (not_6_out, op[0]);
  not not_7 (not_7_out, op[5]);
  not not_8 (not_8_out, op[4]);
  not not_9 (not_9_out, op[1]);
  not not_10 (not_10_out, op[5]);
  not not_11 (not_11_out, op[4]);
  not not_12 (not_12_out, op[2]);
  not not_13 (not_13_out, op[0]);
  not not_14 (not_14_out, op[5]);
  not not_15 (not_15_out, op[4]);
  not not_16 (not_16_out, op[1]);
  not not_17 (not_17_out, op[4]);
  not not_18 (not_18_out, op[2]);
  Counter_part #(.width(16), .max('hffff)) counter_1 (
    .Q(counter_1_q), .clk(clock));  // open: load, D, count, carry, clr
  and and_1 (and_1_out, not_1_out, not_2_out, not_3_out, not_4_out, not_5_out, not_6_out);
  and and_2 (and_2_out, not_7_out, not_8_out, op[2], not_9_out);
  and and_3 (and_3_out, not_10_out, not_11_out, op[3], not_12_out, not_13_out);
  and and_4 (and_4_out, not_14_out, not_15_out, op[3], not_16_out);
  and and_5 (and_5_out, op[5], not_17_out, not_18_out, op[1], op[0]);
  not not_19 (not_19_out, op[5]);
  not not_20 (not_20_out, op[4]);
  not not_21 (not_21_out, op[3]);
  not not_22 (not_22_out, op[2]);
  Counter_part #(.width(16), .max('hffff)) counter_2 (
    .count(and_1_out), .Q(counter_2_q), .clk(clock));  // open: load, D, carry, clr
  or or_1 (or_1_out, and_2_out, and_3_out, and_4_out, and_5_out);
  and and_6 (and_6_out, not_19_out, not_20_out, not_21_out, not_22_out, op[1]);
  Adder #(.width(16)) adder_1 (.a(counter_1_q), .b(16'h1), .out(adder_1_out));  // open: cin, cout
  Adder #(.width(16)) adder_2 (.a(counter_2_q), .b(16'h1), .out(adder_2_out));  // open: cin, cout
  Counter_part #(.width(16), .max('hffff)) counter_3 (
    .count(or_1_out), .Q(I_type), .clk(clock));  // open: load, D, carry, clr
  Counter_part #(.width(16), .max('hffff)) counter_4 (
    .count(and_6_out), .Q(J_type), .clk(clock));  // open: load, D, carry, clr
  Multiplexer #(.width(16), .enable("false")) multiplexer_1 (
    .in0(counter_1_q), .in1(adder_1_out), .out(ALL), .sel(in_3));
  Multiplexer #(.width(16), .enable("false")) multiplexer_2 (
    .in0(counter_2_q), .in1(adder_2_out), .out(R_type), .sel(in_3));

  // Other names for the same wires on the sheet: syscall = in_3
endmodule

module IF_ID (
  input  EN,
  input  branch,
  input  [31:0] PCin,
  input  [31:0] IRin,
  input  Clock,
  output [31:0] PCout,
  output [31:0] IRout
);

  Register #(.width(32)) register_1 (.D(PCin), .en(EN), .Q(PCout), .clk(Clock), .clr(branch));
  Register #(.width(32)) register_2 (.D(IRin), .en(EN), .Q(IRout), .clk(Clock), .clr(branch));
endmodule

module ID_EX (
  input  RS,
  input  [31:0] PCin,
  input  RT,
  input  [31:0] IR,
  input  RegWrite,
  input  [1:0] W_op,
  input  [31:0] D1,
  input  [1:0] Dinop,
  input  [31:0] D2,
  input  MemWrite,
  input  [1:0] PCop,
  input  [31:0] IR15_0,
  input  [3:0] ALUop,
  input  [31:0] IR10_6,
  input  [1:0] AluScrB,
  input  [4:0] rs_2,
  input  AluScrA,
  input  [4:0] rt_2,
  input  syscall,
  input  [4:0] rd,
  input  ERET,
  input  hazard,
  input  branch,
  input  Clock,
  output RS_3,
  output [31:0] PCout,
  output RT_3,
  output [31:0] IR_2,
  output RegWrite_2,
  output [1:0] W_op_2,
  output [31:0] D1out,
  output [1:0] Dinop_2,
  output [31:0] D2out,
  output MemWrite_2,
  output [1:0] PCop_2,
  output [31:0] IR15_0_2,
  output [3:0] ALUop_2,
  output [31:0] IR10_6_2,
  output [1:0] AluScrB_2,
  output [4:0] rs_4,
  output AluScrA_2,
  output [4:0] rt_4,
  output syscall_2,
  output [4:0] rd_2,
  output ERET_2
);

  wire or_1_out;

  Register #(.width(32)) register_1 (.D(PCin), .Q(PCout), .clk(Clock), .clr(or_1_out));  // open: en
  Register #(.width(32)) register_2 (.D(IR), .Q(IR_2), .clk(Clock), .clr(or_1_out));  // open: en
  Register #(.width(32)) register_3 (.D(D1), .Q(D1out), .clk(Clock), .clr(or_1_out));  // open: en
  Register #(.width(32)) register_4 (.D(D2), .Q(D2out), .clk(Clock), .clr(or_1_out));  // open: en
  Register #(.width(32)) register_5 (.D(IR15_0), .Q(IR15_0_2), .clk(Clock), .clr(or_1_out));  // open: en
  Register #(.width(32)) register_6 (.D(IR10_6), .Q(IR10_6_2), .clk(Clock), .clr(or_1_out));  // open: en
  Register #(.width(5)) register_7 (.D(rs_2), .Q(rs_4), .clk(Clock), .clr(or_1_out));  // open: en
  Register #(.width(5)) register_8 (.D(rt_2), .Q(rt_4), .clk(Clock), .clr(or_1_out));  // open: en
  Register #(.width(5)) register_9 (.D(rd), .Q(rd_2), .clk(Clock), .clr(or_1_out));  // open: en
  or or_1 (or_1_out, hazard, branch);
  Register #(.width(1)) register_10 (.D(RS), .Q(RS_3), .clk(Clock), .clr(or_1_out));  // open: en
  Register #(.width(1)) register_11 (.D(RT), .Q(RT_3), .clk(Clock), .clr(or_1_out));  // open: en
  Register #(.width(1)) register_12 (.D(RegWrite), .Q(RegWrite_2), .clk(Clock), .clr(or_1_out));  // open: en
  Register #(.width(2)) register_13 (.D(W_op), .Q(W_op_2), .clk(Clock), .clr(or_1_out));  // open: en
  Register #(.width(2)) register_14 (.D(Dinop), .Q(Dinop_2), .clk(Clock), .clr(or_1_out));  // open: en
  Register #(.width(1)) register_15 (.D(MemWrite), .Q(MemWrite_2), .clk(Clock), .clr(or_1_out));  // open: en
  Register #(.width(2)) register_16 (.D(PCop), .Q(PCop_2), .clk(Clock), .clr(or_1_out));  // open: en
  Register #(.width(4)) register_17 (.D(ALUop), .Q(ALUop_2), .clk(Clock), .clr(or_1_out));  // open: en
  Register #(.width(2)) register_18 (.D(AluScrB), .Q(AluScrB_2), .clk(Clock), .clr(or_1_out));  // open: en
  Register #(.width(1)) register_19 (.D(AluScrA), .Q(AluScrA_2), .clk(Clock), .clr(or_1_out));  // open: en
  Register #(.width(1)) register_20 (.D(syscall), .Q(syscall_2), .clk(Clock), .clr(or_1_out));  // open: en
  Register #(.width(1)) register_21 (.D(ERET), .Q(ERET_2), .clk(Clock), .clr(or_1_out));  // open: en
endmodule

module EX_MEM (
  input  [31:0] PCin,
  input  [31:0] IR,
  input  [31:0] ALU,
  input  [1:0] W_op,
  input  RegWrite,
  input  [31:0] D2,
  input  MemWrite,
  input  [4:0] rs,
  input  syscall,
  input  [4:0] rt,
  input  [1:0] Dinop,
  input  [4:0] rd,
  input  ERET,
  input  Clock,
  output [31:0] PCout,
  output [31:0] IR_2,
  output [31:0] ALU_2,
  output [1:0] W_op_2,
  output RegWrite_2,
  output [31:0] D2_2,
  output MemWrite_2,
  output [4:0] rs_2,
  output syscall_2,
  output [4:0] rt_2,
  output [1:0] Dinop_2,
  output [4:0] rd_2,
  output ERET_2
);

  Register #(.width(32)) register_1 (.D(PCin), .Q(PCout), .clk(Clock));  // open: en, clr
  Register #(.width(32)) register_2 (.D(IR), .Q(IR_2), .clk(Clock));  // open: en, clr
  Register #(.width(32)) register_3 (.D(ALU), .Q(ALU_2), .clk(Clock));  // open: en, clr
  Register #(.width(32)) register_4 (.D(D2), .Q(D2_2), .clk(Clock));  // open: en, clr
  Register #(.width(5)) register_5 (.D(rs), .Q(rs_2), .clk(Clock));  // open: en, clr
  Register #(.width(5)) register_6 (.D(rt), .Q(rt_2), .clk(Clock));  // open: en, clr
  Register #(.width(5)) register_7 (.D(rd), .Q(rd_2), .clk(Clock));  // open: en, clr
  Register #(.width(2)) register_8 (.D(W_op), .Q(W_op_2), .clk(Clock));  // open: en, clr
  Register #(.width(1)) register_9 (.D(RegWrite), .Q(RegWrite_2), .clk(Clock));  // open: en, clr
  Register #(.width(1)) register_10 (.D(MemWrite), .Q(MemWrite_2), .clk(Clock));  // open: en, clr
  Register #(.width(1)) register_11 (.D(syscall), .Q(syscall_2), .clk(Clock));  // open: en, clr
  Register #(.width(2)) register_12 (.D(Dinop), .Q(Dinop_2), .clk(Clock));  // open: en, clr
  Register #(.width(1)) register_13 (.D(ERET), .Q(ERET_2), .clk(Clock));  // open: en, clr
endmodule

module MEM_WB (
  input  [31:0] PCin,
  input  [31:0] IR,
  input  [31:0] Data,
  input  [31:0] ALU,
  input  RegWrite,
  input  [4:0] rs,
  input  [1:0] Dinop,
  input  [4:0] rt,
  input  [1:0] W_op,
  input  [4:0] rd,
  input  Halt,
  input  Clock,
  output [31:0] PCout,
  output [31:0] IR_2,
  output [31:0] Data_2,
  output [31:0] ALU_2,
  output RegWrite_2,
  output [4:0] rs_2,
  output [1:0] Dinop_2,
  output [4:0] rt_2,
  output [1:0] W_op_2,
  output [4:0] rd_2,
  output Halt_2
);

  Register #(.width(32)) register_1 (.D(PCin), .Q(PCout), .clk(Clock));  // open: en, clr
  Register #(.width(32)) register_2 (.D(IR), .Q(IR_2), .clk(Clock));  // open: en, clr
  Register #(.width(32)) register_3 (.D(Data), .Q(Data_2), .clk(Clock));  // open: en, clr
  Register #(.width(32)) register_4 (.D(ALU), .Q(ALU_2), .clk(Clock));  // open: en, clr
  Register #(.width(5)) register_5 (.D(rs), .Q(rs_2), .clk(Clock));  // open: en, clr
  Register #(.width(5)) register_6 (.D(rt), .Q(rt_2), .clk(Clock));  // open: en, clr
  Register #(.width(5)) register_7 (.D(rd), .Q(rd_2), .clk(Clock));  // open: en, clr
  Register #(.width(1)) register_8 (.D(RegWrite), .Q(RegWrite_2), .clk(Clock));  // open: en, clr
  Register #(.width(2)) register_9 (.D(Dinop), .Q(Dinop_2), .clk(Clock));  // open: en, clr
  Register #(.width(2)) register_10 (.D(W_op), .Q(W_op_2), .clk(Clock));  // open: en, clr
  Register #(.width(1)) register_11 (.D(Halt), .Q(Halt_2), .clk(Clock));  // open: en, clr
endmodule

module Translator (
  input  [31:0] IR,
  input  ERET,
  input  exe,
  input  [4:0] rd,
  input  [4:0] rt,
  input  [1:0] W_op,
  output [4:0] R1_num,
  output [4:0] R2_num,
  output [4:0] W_num
);

  wire or_1_out;

  Multiplexer #(.select(2), .width(5), .enable("false")) multiplexer_1 (
    .in0(rd), .in1({5{1'b1}}), .in2(rt), .in3({5{1'b1}}), .out(W_num), .sel(W_op));
  or or_1 (or_1_out, ERET, exe);
  Multiplexer #(.width(5), .enable("false")) multiplexer_2 (
    .in0(IR[20:16]), .in1(5'b11100), .out(R2_num), .sel(or_1_out));

  assign R1_num = IR[25:21];
endmodule

module NPC (
  input  [31:0] PC_4,
  input  [31:0] PC,
  input  [31:0] IMM16,
  input  [31:0] IR,
  input  Equal,
  input  [31:0] D1,
  input  [1:0] PCop,
  input  ERET,
  input  exe,
  input  [31:0] MEM,
  output success,
  output [31:0] NPC
);

  wire [31:0] alu_1_p4, multiplexer_1_out, multiplexer_2_out, multiplexer_3_out, shifter_1_out;

  Shifter #(.width(32)) shifter_1 (.in(IMM16), .\dist (5'b00010), .out(shifter_1_out));
  // ALU alu_1: pin names not known; wires that end beside it: PC, shifter_1_out, 4'b0101, alu_1_p4
  xor xor_1 (success, IR[26], Equal);
  Multiplexer #(.width(32), .enable("false")) multiplexer_1 (
    .in0(PC_4), .in1(alu_1_p4), .out(multiplexer_1_out), .sel(success));
  Multiplexer #(.select(2), .width(32), .enable("false")) multiplexer_2 (
    .in0(PC_4), .in1(multiplexer_1_out), .in2({PC[31:28], IR[25:0], 2'b00}), .in3(D1),
    .out(multiplexer_2_out), .sel(PCop));
  Multiplexer #(.width(32), .enable("false")) multiplexer_3 (
    .in0(multiplexer_2_out), .in1(MEM), .out(multiplexer_3_out), .sel(ERET));
  Multiplexer #(.width(32), .enable("false")) multiplexer_4 (
    .in0(multiplexer_3_out), .in1(32'h3038), .out(NPC), .sel(exe));
endmodule

module Hazard (
  input  RS,
  input  RT,
  input  RegWriteM,
  input  [4:0] rsE,
  input  [4:0] rdM,
  input  [4:0] rtM,
  input  [1:0] W_opM,
  input  [4:0] rtE,
  input  RegWriteW,
  input  [4:0] rdW,
  input  [4:0] rtW,
  input  [1:0] W_opW,
  input  MemToRegE,
  input  [4:0] rsD,
  input  [4:0] rtD,
  input  [1:0] PCop,
  input  success,
  output [1:0] ForwardAE,
  output [1:0] ForwardBE,
  output FlushE,
  output BranchHazard
);

  wire and_1_out, comparator_1_eq, comparator_2_eq, comparator_3_eq, comparator_4_eq, comparator_5_eq,
       comparator_6_eq, comparator_7_eq, comparator_8_eq, multiplexer_3_out, multiplexer_4_out,
       multiplexer_5_out, multiplexer_6_out, or_1_out;
  wire [4:0] multiplexer_1_out, multiplexer_2_out;

  Multiplexer #(.select(2), .width(5), .enable("false")) multiplexer_1 (
    .in0(rdM), .in1({5{1'b1}}), .in2(rtM), .in3({5{1'b1}}), .out(multiplexer_1_out), .sel(W_opM));
  Multiplexer #(.select(2), .width(5), .enable("false")) multiplexer_2 (
    .in0(rdW), .in1({5{1'b1}}), .in2(rtW), .in3({5{1'b1}}), .out(multiplexer_2_out), .sel(W_opW));
  Comparator #(.width(5)) comparator_1 (.a(rsE), .b(multiplexer_1_out), .eq(comparator_1_eq));  // open: gt, lt
  Comparator #(.width(5)) comparator_2 (.a({5{1'b0}}), .b(multiplexer_1_out), .eq(comparator_2_eq));  // open: gt, lt
  Comparator #(.width(5)) comparator_3 (.a(multiplexer_1_out), .b(rtE), .eq(comparator_3_eq));  // open: gt, lt
  Comparator #(.width(5)) comparator_4 (.a(rsE), .b(multiplexer_2_out), .eq(comparator_4_eq));  // open: gt, lt
  Comparator #(.width(5)) comparator_5 (.a({5{1'b0}}), .b(multiplexer_2_out), .eq(comparator_5_eq));  // open: gt, lt
  Comparator #(.width(5)) comparator_6 (.a(multiplexer_2_out), .b(rtE), .eq(comparator_6_eq));  // open: gt, lt
  Comparator #(.width(5)) comparator_7 (.a(rtE), .b(rsD), .eq(comparator_7_eq));  // open: gt, lt
  Comparator #(.width(5)) comparator_8 (.a(rtE), .b(rtD), .eq(comparator_8_eq));  // open: gt, lt
  Multiplexer #(.enable("false")) multiplexer_3 (.in0(1'b0), .in1(comparator_1_eq), .out(multiplexer_3_out), .sel(RS));
  Multiplexer #(.enable("false")) multiplexer_4 (.in0(1'b0), .in1(comparator_3_eq), .out(multiplexer_4_out), .sel(RT));
  Multiplexer #(.enable("false")) multiplexer_5 (.in0(1'b0), .in1(comparator_4_eq), .out(multiplexer_5_out), .sel(RS));
  Multiplexer #(.enable("false")) multiplexer_6 (.in0(1'b0), .in1(comparator_6_eq), .out(multiplexer_6_out), .sel(RT));
  or or_1 (or_1_out, comparator_7_eq, comparator_8_eq);
  and and_1 (and_1_out, ~PCop[1], PCop[0], success);  // AND_Gate
  and and_2 (ForwardAE[1], RegWriteM, multiplexer_3_out, ~comparator_2_eq);  // AND_Gate
  and and_3 (ForwardBE[1], ~comparator_2_eq, multiplexer_4_out, RegWriteM);  // AND_Gate
  and and_4 (ForwardAE[0], RegWriteW, multiplexer_5_out, ~comparator_5_eq);  // AND_Gate
  and and_5 (ForwardBE[0], ~comparator_5_eq, multiplexer_6_out, RegWriteW);  // AND_Gate
  and and_6 (FlushE, MemToRegE, or_1_out);
  or or_2 (BranchHazard, PCop[1], and_1_out);
endmodule

module Counter (
  input  LOCK,
  input  clock,
  input  syscall,
  output [15:0] BUb,
  output [15:0] Per
);

  wire [15:0] adder_1_out, counter_2_q;

  Counter_part #(.width(16), .max('hffff)) counter_1 (.count(LOCK), .Q(BUb), .clk(clock));  // open: load, D, carry, clr
  Counter_part #(.width(16), .max('hffff)) counter_2 (
    .Q(counter_2_q), .clk(clock));  // open: load, D, count, carry, clr
  Adder #(.width(16)) adder_1 (.a(counter_2_q), .b(16'h1), .out(adder_1_out));  // open: cin, cout
  Multiplexer #(.width(16), .enable("false")) multiplexer_1 (
    .in0(counter_2_q), .in1(adder_1_out), .out(Per), .sel(syscall));
endmodule
