// Logisim project Regfile.circ as structural Verilog: 1 circuit, main circuit main
module main (
  input  [4:0] Reg1_num,
  input  [4:0] Reg2,
  input  [4:0] Write_Reg_num,
  input  [31:0] Din,
  input  Write_Enable,
  input  Clock,
  output [31:0] Reg1,
  output [31:0] s0_Value,
  output [31:0] s1_Value,
  output [31:0] s2_Value,
  output [31:0] ra_Value,
  output [31:0] Reg2_2
);

  wire en1, en2, en3, en4, en5, en6, en7, en8, en9, en10, en11, en12, en13, en14, en15, en16, en17, en18,
       en19, en20, en21, en22, en23, en24, en25, en26, en27, en28, en29, en30, en31;
  wire [31:0] in1, in2, in3, in4, in5, in6, in7, in8, in9, in10, in11, in12, in13, in14, in15, in16, in17,
       in18, in19, in20, in21, in22, in23, in24, in25, in26, in27, in28, in29, in30, in31, out0, out1, out3,
       out5, out6, out7, out8, out9, out10, out11, out12, out13, out14, out15, out18, out19, out20, out21,
       out22, out23, out24, out25, out26, out27, out28, out29, out30, out31;

  Register #(.width(32)) reg0 (.Q(out0));  // open: D, en, clk, clr
  Register #(.width(32)) reg8 (.D(in8), .en(en8), .Q(out8), .clk(Clock));  // open: clr
  Register #(.width(32)) reg16 (.D(in16), .en(en16), .Q(s0_Value), .clk(Clock));  // open: clr
  Register #(.width(32)) reg24 (.D(in24), .en(en24), .Q(out24), .clk(Clock));  // open: clr
  Register #(.width(32)) u_reg1 (.D(in1), .en(en1), .Q(out1), .clk(Clock));  // open: clr
  Register #(.width(32)) reg9 (.D(in9), .en(en9), .Q(out9), .clk(Clock));  // open: clr
  Register #(.width(32)) reg17 (.D(in17), .en(en17), .Q(s1_Value), .clk(Clock));  // open: clr
  Register #(.width(32)) reg25 (.D(in25), .en(en25), .Q(out25), .clk(Clock));  // open: clr
  Register #(.width(32)) u_reg2 (.D(in2), .en(en2), .Q(s2_Value), .clk(Clock));  // open: clr
  Register #(.width(32)) reg10 (.D(in10), .en(en10), .Q(out10), .clk(Clock));  // open: clr
  Register #(.width(32)) reg18 (.D(in18), .en(en18), .Q(out18), .clk(Clock));  // open: clr
  Register #(.width(32)) reg26 (.D(in26), .en(en26), .Q(out26), .clk(Clock));  // open: clr
  Register #(.width(32)) reg3 (.D(in3), .en(en3), .Q(out3), .clk(Clock));  // open: clr
  Register #(.width(32)) reg11 (.D(in11), .en(en11), .Q(out11), .clk(Clock));  // open: clr
  Register #(.width(32)) reg19 (.D(in19), .en(en19), .Q(out19), .clk(Clock));  // open: clr
  Register #(.width(32)) reg27 (.D(in27), .en(en27), .Q(out27), .clk(Clock));  // open: clr
  Demultiplexer #(.select(5), .enable("false")) demultiplexer_1 (
    .out1(en1), .out2(en2), .out3(en3), .out4(en4), .out5(en5), .out6(en6), .out7(en7), .out8(en8),
    .out9(en9), .out10(en10), .out11(en11), .out12(en12), .out13(en13), .out14(en14), .out15(en15),
    .out16(en16), .out17(en17), .out18(en18), .out19(en19), .out20(en20), .out21(en21), .out22(en22),
    .out23(en23), .out24(en24), .out25(en25), .out26(en26), .out27(en27), .out28(en28), .out29(en29),
    .out30(en30), .out31(en31), .in(Write_Enable), .sel(Write_Reg_num));  // open: out0
  Demultiplexer #(.select(5), .width(32)) demultiplexer_2 (
    .out1(in1), .out2(in2), .out3(in3), .out4(in4), .out5(in5), .out6(in6), .out7(in7), .out8(in8),
    .out9(in9), .out10(in10), .out11(in11), .out12(in12), .out13(in13), .out14(in14), .out15(in15),
    .out16(in16), .out17(in17), .out18(in18), .out19(in19), .out20(in20), .out21(in21), .out22(in22),
    .out23(in23), .out24(in24), .out25(in25), .out26(in26), .out27(in27), .out28(in28), .out29(in29),
    .out30(in30), .out31(in31), .in(Din), .sel(Write_Reg_num), .en(Write_Enable));  // open: out0
  Multiplexer #(.select(5), .width(32), .enable("false")) multiplexer_1 (
    .in0(out0), .in1(out1), .in2(s2_Value), .in3(out3), .in4(ra_Value), .in5(out5), .in6(out6), .in7(out7),
    .in8(out8), .in9(out9), .in10(out10), .in11(out11), .in12(out12), .in13(out13), .in14(out14),
    .in15(out15), .in16(s0_Value), .in17(s1_Value), .in18(out18), .in19(out19), .in20(out20), .in21(out21),
    .in22(out22), .in23(out23), .in24(out24), .in25(out25), .in26(out26), .in27(out27), .in28(out28),
    .in29(out29), .in30(out30), .in31(out31), .out(Reg1), .sel(Reg1_num));
  Multiplexer #(.select(5), .width(32), .enable("false")) multiplexer_2 (
    .in0(out0), .in1(out1), .in2(s2_Value), .in3(out3), .in4(ra_Value), .in5(out5), .in6(out6), .in7(out7),
    .in8(out8), .in9(out9), .in10(out10), .in11(out11), .in12(out12), .in13(out13), .in14(out14),
    .in15(out15), .in16(s0_Value), .in17(s1_Value), .in18(out18), .in19(out19), .in20(out20), .in21(out21),
    .in22(out22), .in23(out23), .in24(out24), .in25(out25), .in26(out26), .in27(out27), .in28(out28),
    .in29(out29), .in30(out30), .in31(out31), .out(Reg2_2), .sel(Reg2));
  Register #(.width(32)) reg4 (.D(in4), .en(en4), .Q(ra_Value), .clk(Clock));  // open: clr
  Register #(.width(32)) reg12 (.D(in12), .en(en12), .Q(out12), .clk(Clock));  // open: clr
  Register #(.width(32)) reg20 (.D(in20), .en(en20), .Q(out20), .clk(Clock));  // open: clr
  Register #(.width(32)) reg28 (.D(in28), .en(en28), .Q(out28), .clk(Clock));  // open: clr
  Register #(.width(32)) reg5 (.D(in5), .en(en5), .Q(out5), .clk(Clock));  // open: clr
  Register #(.width(32)) reg13 (.D(in13), .en(en13), .Q(out13), .clk(Clock));  // open: clr
  Register #(.width(32)) reg21 (.D(in21), .en(en21), .Q(out21), .clk(Clock));  // open: clr
  Register #(.width(32)) reg29 (.D(in29), .en(en29), .Q(out29), .clk(Clock));  // open: clr
  Register #(.width(32)) reg6 (.D(in6), .en(en6), .Q(out6), .clk(Clock));  // open: clr
  Register #(.width(32)) reg14 (.D(in14), .en(en14), .Q(out14), .clk(Clock));  // open: clr
  Register #(.width(32)) reg22 (.D(in22), .en(en22), .Q(out22), .clk(Clock));  // open: clr
  Register #(.width(32)) reg30 (.D(in30), .en(en30), .Q(out30), .clk(Clock));  // open: clr
  Register #(.width(32)) reg7 (.D(in7), .en(en7), .Q(out7), .clk(Clock));  // open: clr
  Register #(.width(32)) reg15 (.D(in15), .en(en15), .Q(out15), .clk(Clock));  // open: clr
  Register #(.width(32)) reg23 (.D(in23), .en(en23), .Q(out23), .clk(Clock));  // open: clr
  Register #(.width(32)) reg31 (.D(in31), .en(en31), .Q(out31), .clk(Clock));  // open: clr

  // Other names for the same wires on the sheet: clk = Clock; out2[31:0] = s2_Value; s2[31:0] = s2_Value;
  //   out4[31:0] = ra_Value; ra[31:0] = ra_Value; out16[31:0] = s0_Value; s0[31:0] = s0_Value; out17[31:0] = s1_Value;
  //   s1[31:0] = s1_Value; reg2_num[4:0] = Reg2; reg2_t[31:0] = Reg2_2; WE = Write_Enable; write_data[31:0] = Din

  // Notes on the sheet:
  //   输入引脚
  //   输出引脚
  //   请在下方利用上方输入输出引脚的隧道信号构建ALU电路，ctrl+d复制选择部件
  //   Debug引脚，便于观测寄存器值
  //   请勿修改引脚以及封装，直接使用隧道连接电路
endmodule
